// Logisim project ALU_Group03.circ as structural Verilog: 7 circuits, main circuit main
module main (
  output halt,
  output [6:0] counter,
  output [3:0] op,
  output [15:0] a,
  output [15:0] b,
  output [15:0] oracle,
  output [15:0] result,
  output err_oracle,
  output error,
  output ok,
  output start_delimiter
);

  wire and_1_out, and_2_out, clock_1_out, comparator_1_eq, comparator_2_eq;

  Clock clock_1 (.out(clock_1_out));
  Counter #(.width(7), .max('h7f), .trigger("falling")) counter_1 (
    .Q(counter), .carry(halt), .clk(clock_1_out));  // open: load, D, count, clr
  RAM #(.addrWidth(10), .dataWidth(4), .bus("separate")) ram_1 (
    .addr({counter, 3'b000}), .data(op), .ld(1'b1));  // open: din, str, sel, clk, clr
  RAM #(.addrWidth(10), .dataWidth(16), .bus("separate")) ram_2 (
    .addr({counter, 3'b001}), .data(a), .ld(1'b1));  // open: din, str, sel, clk, clr
  RAM #(.addrWidth(10), .dataWidth(16), .bus("separate")) ram_3 (
    .addr({counter, 3'b010}), .data(b), .ld(1'b1));  // open: din, str, sel, clk, clr
  RAM #(.addrWidth(10), .dataWidth(16), .bus("separate")) ram_4 (
    .addr({counter, 3'b011}), .data(oracle), .ld(1'b1));  // open: din, str, sel, clk, clr
  RAM #(.addrWidth(10), .dataWidth(1), .bus("separate")) ram_5 (
    .addr({counter, 3'b100}), .data(err_oracle), .ld(1'b1));  // open: din, str, sel, clk, clr
  RAM #(.addrWidth(10), .dataWidth(1), .bus("separate")) ram_6 (
    .addr({counter, 3'b101}), .data(start_delimiter), .ld(1'b1));  // open: din, str, sel, clk, clr
  _16_bit_ALU u_16_bit_alu_1 (.ALU_code(op), .a(a), .b(b), .overflow(error), .result(result));
  Comparator #(.width(1), .mode("unsigned")) comparator_1 (
    .a(error), .b(err_oracle), .eq(comparator_1_eq));  // open: gt, lt
  Comparator #(.width(16)) comparator_2 (.a(result), .b(oracle), .eq(comparator_2_eq));  // open: gt, lt
  and and_1 (and_1_out, comparator_1_eq, error);
  and and_2 (and_2_out, comparator_2_eq, comparator_1_eq, ~error);  // AND_Gate
  or or_1 (ok, and_1_out, and_2_out);

  // Notes on the sheet:
  //   You must complete the circuit '16-bit ALU' instead.
  //   DO NOT EDIT THIS CIRCUIT!
endmodule

module _16_bit_ALU (
  input  [3:0] ALU_code,
  input  [15:0] a,
  input  [15:0] b,
  output overflow,
  output [15:0] result
);

  wire and_1_out, and_2_out, and_3_out, and_4_out, and_5_out, and_6_out, and_7_out, and_8_out, and_9_out,
       and_10_out, Binvert_out_2, equals_1_out_3, n1bit_alu_1_out_7, n1bit_alu_1_out_9, n1bit_alu_1_out_10,
       n1bit_alu_2_out_7, n1bit_alu_2_out_9, n1bit_alu_2_out_10, n1bit_alu_3_out_7, n1bit_alu_3_out_9,
       n1bit_alu_3_out_10, n1bit_alu_4_out_7, n1bit_alu_4_out_9, n1bit_alu_4_out_10, n1bit_alu_5_out_7,
       n1bit_alu_5_out_9, n1bit_alu_5_out_10, n1bit_alu_6_out_7, n1bit_alu_6_out_9, n1bit_alu_6_out_10,
       n1bit_alu_7_out_7, n1bit_alu_7_out_9, n1bit_alu_7_out_10, n1bit_alu_8_out_7, n1bit_alu_8_out_9,
       n1bit_alu_8_out_10, n1bit_alu_9_out_7, n1bit_alu_9_out_9, n1bit_alu_9_out_10, n1bit_alu_10_out_7,
       n1bit_alu_10_out_9, n1bit_alu_10_out_10, n1bit_alu_11_out_7, n1bit_alu_11_out_9, n1bit_alu_11_out_10,
       n1bit_alu_12_out_7, n1bit_alu_12_out_9, n1bit_alu_12_out_10, n1bit_alu_13_out_7, n1bit_alu_13_out_9,
       n1bit_alu_13_out_10, n1bit_alu_14_out_7, n1bit_alu_14_out_9, n1bit_alu_14_out_10, n1bit_alu_15_out_7,
       n1bit_alu_15_out_9, n1bit_alu_15_out_10, n1bit_alu_16_out_7, not_1_out, or_1_out, or_2_out, or_3_out,
       or_4_out;
  wire [15:0] bit_extender_1_out, bit_extender_2_out, bit_extender_3_out, n1bit_alu_1_out_8;

  Binvert Binvert (.ALU_code(ALU_code), .out_2(Binvert_out_2));
  _1Bit_ALU u_1bit_alu_1 (
    .a(a[0]), .b(b[0]), .Carry_In(Binvert_out_2), .selector(ALU_code), .out_8(n1bit_alu_1_out_8[0]),
    .Previous_bit(1'b0), .out_7(n1bit_alu_1_out_7), .Next_bit(n1bit_alu_2_out_7), .out_9(n1bit_alu_1_out_9),
    .out_10(n1bit_alu_1_out_10));
  _1Bit_ALU u_1bit_alu_2 (
    .a(a[1]), .b(b[1]), .Carry_In(n1bit_alu_1_out_10), .selector(ALU_code), .out_8(n1bit_alu_1_out_8[1]),
    .Previous_bit(n1bit_alu_1_out_9), .out_7(n1bit_alu_2_out_7), .Next_bit(n1bit_alu_3_out_7),
    .out_9(n1bit_alu_2_out_9), .out_10(n1bit_alu_2_out_10));
  _1Bit_ALU u_1bit_alu_3 (
    .a(a[2]), .b(b[2]), .Carry_In(n1bit_alu_2_out_10), .selector(ALU_code), .out_8(n1bit_alu_1_out_8[2]),
    .Previous_bit(n1bit_alu_2_out_9), .out_7(n1bit_alu_3_out_7), .Next_bit(n1bit_alu_4_out_7),
    .out_9(n1bit_alu_3_out_9), .out_10(n1bit_alu_3_out_10));
  _1Bit_ALU u_1bit_alu_4 (
    .a(a[3]), .b(b[3]), .Carry_In(n1bit_alu_3_out_10), .selector(ALU_code), .out_8(n1bit_alu_1_out_8[3]),
    .Previous_bit(n1bit_alu_3_out_9), .out_7(n1bit_alu_4_out_7), .Next_bit(n1bit_alu_5_out_7),
    .out_9(n1bit_alu_4_out_9), .out_10(n1bit_alu_4_out_10));
  _1Bit_ALU u_1bit_alu_5 (
    .a(a[4]), .b(b[4]), .Carry_In(n1bit_alu_4_out_10), .selector(ALU_code), .out_8(n1bit_alu_1_out_8[4]),
    .Previous_bit(n1bit_alu_4_out_9), .out_7(n1bit_alu_5_out_7), .Next_bit(n1bit_alu_6_out_7),
    .out_9(n1bit_alu_5_out_9), .out_10(n1bit_alu_5_out_10));
  _1Bit_ALU u_1bit_alu_6 (
    .a(a[5]), .b(b[5]), .Carry_In(n1bit_alu_5_out_10), .selector(ALU_code), .out_8(n1bit_alu_1_out_8[5]),
    .Previous_bit(n1bit_alu_5_out_9), .out_7(n1bit_alu_6_out_7), .Next_bit(n1bit_alu_7_out_7),
    .out_9(n1bit_alu_6_out_9), .out_10(n1bit_alu_6_out_10));
  _1Bit_ALU u_1bit_alu_7 (
    .a(a[6]), .b(b[6]), .Carry_In(n1bit_alu_6_out_10), .selector(ALU_code), .out_8(n1bit_alu_1_out_8[6]),
    .Previous_bit(n1bit_alu_6_out_9), .out_7(n1bit_alu_7_out_7), .Next_bit(n1bit_alu_8_out_7),
    .out_9(n1bit_alu_7_out_9), .out_10(n1bit_alu_7_out_10));
  _1Bit_ALU u_1bit_alu_8 (
    .a(a[7]), .b(b[7]), .Carry_In(n1bit_alu_7_out_10), .selector(ALU_code), .out_8(n1bit_alu_1_out_8[7]),
    .Previous_bit(n1bit_alu_7_out_9), .out_7(n1bit_alu_8_out_7), .Next_bit(n1bit_alu_9_out_7),
    .out_9(n1bit_alu_8_out_9), .out_10(n1bit_alu_8_out_10));
  _1Bit_ALU u_1bit_alu_9 (
    .a(a[8]), .b(b[8]), .Carry_In(n1bit_alu_8_out_10), .selector(ALU_code), .out_8(n1bit_alu_1_out_8[8]),
    .Previous_bit(n1bit_alu_8_out_9), .out_7(n1bit_alu_9_out_7), .Next_bit(n1bit_alu_10_out_7),
    .out_9(n1bit_alu_9_out_9), .out_10(n1bit_alu_9_out_10));
  _1Bit_ALU u_1bit_alu_10 (
    .a(a[9]), .b(b[9]), .Carry_In(n1bit_alu_9_out_10), .selector(ALU_code), .out_8(n1bit_alu_1_out_8[9]),
    .Previous_bit(n1bit_alu_9_out_9), .out_7(n1bit_alu_10_out_7), .Next_bit(n1bit_alu_11_out_7),
    .out_9(n1bit_alu_10_out_9), .out_10(n1bit_alu_10_out_10));
  _1Bit_ALU u_1bit_alu_11 (
    .a(a[10]), .b(b[10]), .Carry_In(n1bit_alu_10_out_10), .selector(ALU_code), .out_8(n1bit_alu_1_out_8[10]),
    .Previous_bit(n1bit_alu_10_out_9), .out_7(n1bit_alu_11_out_7), .Next_bit(n1bit_alu_12_out_7),
    .out_9(n1bit_alu_11_out_9), .out_10(n1bit_alu_11_out_10));
  _1Bit_ALU u_1bit_alu_12 (
    .a(a[11]), .b(b[11]), .Carry_In(n1bit_alu_11_out_10), .selector(ALU_code), .out_8(n1bit_alu_1_out_8[11]),
    .Previous_bit(n1bit_alu_11_out_9), .out_7(n1bit_alu_12_out_7), .Next_bit(n1bit_alu_13_out_7),
    .out_9(n1bit_alu_12_out_9), .out_10(n1bit_alu_12_out_10));
  _1Bit_ALU u_1bit_alu_13 (
    .a(a[12]), .b(b[12]), .Carry_In(n1bit_alu_12_out_10), .selector(ALU_code), .out_8(n1bit_alu_1_out_8[12]),
    .Previous_bit(n1bit_alu_12_out_9), .out_7(n1bit_alu_13_out_7), .Next_bit(n1bit_alu_14_out_7),
    .out_9(n1bit_alu_13_out_9), .out_10(n1bit_alu_13_out_10));
  _1Bit_ALU u_1bit_alu_14 (
    .a(a[13]), .b(b[13]), .Carry_In(n1bit_alu_13_out_10), .selector(ALU_code), .out_8(n1bit_alu_1_out_8[13]),
    .Previous_bit(n1bit_alu_13_out_9), .out_7(n1bit_alu_14_out_7), .Next_bit(n1bit_alu_15_out_7),
    .out_9(n1bit_alu_14_out_9), .out_10(n1bit_alu_14_out_10));
  _1Bit_ALU u_1bit_alu_15 (
    .a(a[14]), .b(b[14]), .Carry_In(n1bit_alu_14_out_10), .selector(ALU_code), .out_8(n1bit_alu_1_out_8[14]),
    .Previous_bit(n1bit_alu_14_out_9), .out_7(n1bit_alu_15_out_7), .Next_bit(n1bit_alu_16_out_7),
    .out_9(n1bit_alu_15_out_9), .out_10(n1bit_alu_15_out_10));
  _1Bit_ALU u_1bit_alu_16 (
    .a(a[15]), .b(b[15]), .Carry_In(n1bit_alu_15_out_10), .selector(ALU_code), .out_8(n1bit_alu_1_out_8[15]),
    .Previous_bit(n1bit_alu_15_out_9), .out_7(n1bit_alu_16_out_7), .Next_bit(a[15]));  // open: out_9, out_10
  and and_1 (and_1_out, n1bit_alu_1_out_8[0], n1bit_alu_1_out_8[1], n1bit_alu_1_out_8[2], n1bit_alu_1_out_8[3], n1bit_alu_1_out_8[4], n1bit_alu_1_out_8[5], n1bit_alu_1_out_8[6], n1bit_alu_1_out_8[7], n1bit_alu_1_out_8[8], n1bit_alu_1_out_8[9], n1bit_alu_1_out_8[10], n1bit_alu_1_out_8[11], n1bit_alu_1_out_8[12], n1bit_alu_1_out_8[13], n1bit_alu_1_out_8[14], n1bit_alu_1_out_8[15]);
  or or_1 (or_1_out, and_2_out, n1bit_alu_1_out_8[15]);
  and and_2 (and_2_out, a[15], ~b[15]);  // AND_Gate
  and and_3 (and_3_out, ~a[15], ~b[15], n1bit_alu_1_out_8[15]);  // AND_Gate
  and and_4 (and_4_out, a[15], b[15], ~n1bit_alu_1_out_8[15]);  // AND_Gate
  and and_5 (and_5_out, a[15], ~b[15], ~n1bit_alu_1_out_8[15]);  // AND_Gate
  and and_6 (and_6_out, ~a[15], b[15], n1bit_alu_1_out_8[15]);  // AND_Gate
  and and_7 (and_7_out, a[15], n1bit_alu_1_out_8[15]);
  Equals equals_1 (.A(a[15]), .B(n1bit_alu_1_out_8[15]), .out_3(equals_1_out_3));
  assign bit_extender_1_out = {{15{1'b0}}, and_1_out};  // Bit_Extender bit_extender_1
  and and_8 (and_8_out, ~n1bit_alu_1_out_8[0], ~n1bit_alu_1_out_8[1], ~n1bit_alu_1_out_8[2], ~n1bit_alu_1_out_8[3], ~n1bit_alu_1_out_8[4], ~n1bit_alu_1_out_8[5], ~n1bit_alu_1_out_8[6], ~n1bit_alu_1_out_8[7], ~n1bit_alu_1_out_8[8], ~n1bit_alu_1_out_8[9], ~n1bit_alu_1_out_8[10], ~n1bit_alu_1_out_8[11], ~n1bit_alu_1_out_8[12], ~n1bit_alu_1_out_8[13], ~n1bit_alu_1_out_8[14], ~n1bit_alu_1_out_8[15]);  // AND_Gate
  assign bit_extender_2_out = {{15{1'b0}}, or_1_out};  // Bit_Extender bit_extender_2
  or or_2 (or_2_out, and_9_out, ~n1bit_alu_1_out_8[15]);  // OR_Gate
  and and_9 (and_9_out, ~a[15], b[15]);  // AND_Gate
  or or_3 (or_3_out, and_3_out, and_4_out);
  or or_4 (or_4_out, and_5_out, and_6_out);
  not not_1 (not_1_out, equals_1_out_3);
  and and_10 (and_10_out, ~and_8_out, or_2_out);  // AND_Gate
  assign bit_extender_3_out = {{15{1'b0}}, and_10_out};  // Bit_Extender bit_extender_3
  Multiplexer #(.select(4), .width(16)) multiplexer_1 (
    .in0(n1bit_alu_1_out_8), .in1(n1bit_alu_1_out_8), .in2(n1bit_alu_1_out_8), .in3(n1bit_alu_1_out_8),
    .in4(bit_extender_2_out), .in5(bit_extender_3_out), .in6(bit_extender_1_out), .in7(n1bit_alu_1_out_8),
    .in8(n1bit_alu_1_out_8), .in9(n1bit_alu_1_out_8), .in10(n1bit_alu_1_out_8), .in11(n1bit_alu_1_out_8),
    .in12(n1bit_alu_1_out_8), .in13(n1bit_alu_1_out_8), .in14(n1bit_alu_1_out_8), .in15(n1bit_alu_1_out_8),
    .out(result), .sel(ALU_code));  // open: en
  Multiplexer #(.select(4)) multiplexer_2 (
    .in0(1'b0), .in1(1'b0), .in2(or_3_out), .in3(or_4_out), .in4(1'b0), .in5(1'b0), .in6(1'b0), .in7(1'b0),
    .in8(1'b0), .in9(and_7_out), .in10(not_1_out), .in11(1'b0), .in12(1'b0), .in13(1'b0), .in14(1'b0),
    .in15(1'b0), .out(overflow), .sel(ALU_code));  // open: en

  // Notes on the sheet:
  //   Do not change the circuit appearance.
  //   This circuit is used as a block in the main circuit, and its layout must remain unchanged.
  //   DO NOT CHANGE THE INPUTS AND OUTPUTS OF THIS CIRCUIT!
  //   Do not add/remove inputs or outputs. Do not even change their location or orientation.
endmodule

module _1Bit_ALU (
  input  Previous_bit,
  input  [3:0] selector,
  input  Carry_In,
  input  a,
  input  b,
  input  Next_bit,
  output out_7,
  output out_8,
  output out_9,
  output out_10
);

  wire A_invert_out_2, and_1_out, and_2_out, and_3_out, and_4_out, and_5_out, and_6_out, and_7_out,
       B_invert_out_2, equals_1_out_3, Generic_AND_out, Generic_OR_out, n1_bit_multiplexer_1_out_4,
       n1_bit_multiplexer_2_out_4, n1_bit_multiplexer_3_out_4, not_1_out, not_2_out, not_3_out, or_1_out;

  or Generic_OR (Generic_OR_out, a, b);
  and Generic_AND (Generic_AND_out, a, b);
  _1_bit_multiplexer u_1_bit_multiplexer_1 (
    .A(a), .B(not_1_out), .selector(A_invert_out_2), .out_4(n1_bit_multiplexer_1_out_4));
  not not_1 (not_1_out, a);
  _1_bit_multiplexer u_1_bit_multiplexer_2 (
    .A(b), .B(not_2_out), .selector(B_invert_out_2), .out_4(n1_bit_multiplexer_2_out_4));
  not not_2 (not_2_out, b);
  not not_3 (not_3_out, a);
  _1_bit_multiplexer u_1_bit_multiplexer_3 (
    .A(n1_bit_multiplexer_2_out_4), .B(1'b0), .selector(A_invert_out_2), .out_4(n1_bit_multiplexer_3_out_4));
  Equals equals_1 (.A(b), .B(a), .out_3(equals_1_out_3));
  and and_1 (and_1_out, n1_bit_multiplexer_1_out_4, n1_bit_multiplexer_3_out_4, Carry_In);
  and and_2 (and_2_out, ~n1_bit_multiplexer_1_out_4, ~n1_bit_multiplexer_3_out_4, Carry_In);  // AND_Gate
  and and_3 (and_3_out, n1_bit_multiplexer_1_out_4, ~n1_bit_multiplexer_3_out_4, ~Carry_In);  // AND_Gate
  and and_4 (and_4_out, ~n1_bit_multiplexer_1_out_4, n1_bit_multiplexer_3_out_4, ~Carry_In);  // AND_Gate
  and and_5 (and_5_out, Carry_In, n1_bit_multiplexer_3_out_4);
  and and_6 (and_6_out, Carry_In, n1_bit_multiplexer_1_out_4);
  and and_7 (and_7_out, n1_bit_multiplexer_3_out_4, n1_bit_multiplexer_1_out_4);
  Ainvert A_invert (.out_2(A_invert_out_2), .ALU_code(selector));
  or or_1 (or_1_out, and_1_out, and_2_out, and_3_out, and_4_out);
  or or_2 (out_10, and_5_out, and_6_out, and_7_out);
  Binvert B_invert (.ALU_code(selector), .out_2(B_invert_out_2));
  Multiplexer #(.select(4)) multiplexer_1 (
    .in0(Generic_OR_out), .in1(Generic_AND_out), .in2(or_1_out), .in3(or_1_out), .in4(or_1_out),
    .in5(or_1_out), .in6(equals_1_out_3), .in7(1'b0), .in8(not_3_out), .in9(or_1_out), .in10(Previous_bit),
    .in11(Next_bit), .out(out_8), .sel(selector));  // open: in12, in13, in14, in15, en

  assign out_7 = a;
  assign out_9 = a;
endmodule

module Equals (
  input  A,
  input  B,
  output out_3
);

  wire and_1_out, and_2_out;

  and and_1 (and_1_out, A, B);
  and and_2 (and_2_out, ~A, ~B);  // AND_Gate
  or or_1 (out_3, and_1_out, and_2_out);
endmodule

module Binvert (
  input  [3:0] ALU_code,
  output out_2
);

  wire and_1_out, and_2_out, and_3_out, and_4_out, not_1_out, not_2_out, not_3_out, not_4_out, not_5_out,
       not_6_out, not_7_out;

  not not_1 (not_1_out, ALU_code[2]);
  not not_2 (not_2_out, ALU_code[3]);
  not not_3 (not_3_out, ALU_code[0]);
  not not_4 (not_4_out, ALU_code[1]);
  not not_5 (not_5_out, ALU_code[3]);
  not not_6 (not_6_out, ALU_code[1]);
  not not_7 (not_7_out, ALU_code[3]);
  and and_1 (and_1_out, ALU_code[0], ALU_code[1], not_1_out, not_2_out);
  and and_2 (and_2_out, not_3_out, not_4_out, ALU_code[2], not_5_out);
  and and_3 (and_3_out, ALU_code[0], not_6_out, ALU_code[2], not_7_out);
  and and_4 (and_4_out, ALU_code[0], ~ALU_code[1], ~ALU_code[2], ALU_code[3]);  // AND_Gate
  or or_1 (out_2, and_1_out, and_2_out, and_3_out, and_4_out);
endmodule

module _1_bit_multiplexer (
  input  selector,
  input  A,
  input  B,
  output out_4
);

  wire and_1_out, and_2_out;

  and and_1 (and_1_out, A, ~selector);  // AND_Gate
  and and_2 (and_2_out, B, selector);
  or or_1 (out_4, and_1_out, and_2_out);
endmodule

module Ainvert (
  input  [3:0] ALU_code,
  output out_2
);

  and and_1 (out_2, ALU_code[0], ~ALU_code[1], ~ALU_code[2], ALU_code[3]);  // AND_Gate
endmodule
