// Logisim project FullDataPath.circ as structural Verilog: 7 circuits, main circuit main
module main (
  output [15:0] pc,
  output [15:0] r0,
  output [15:0] r1,
  output [15:0] r2,
  output [15:0] r3,
  output [15:0] r4,
  output [15:0] r5,
  output [15:0] r6,
  output [15:0] r7,
  output [15:0] r8,
  output [15:0] r9,
  output [15:0] r10,
  output [15:0] r11,
  output [15:0] r12,
  output [15:0] r13,
  output [15:0] r14,
  output [15:0] r15,
  output halt
);

  wire and_1_out, and_2_out, and_3_out, clock_1_out, control_1_alusrc, control_1_branchimm,
       control_1_branchrel, control_1_jal, control_1_jump, control_1_memread, control_1_memtoreg,
       control_1_memwrite, control_1_regadress, control_1_regdst, control_1_regwrite, n16_bit_alu_1_overflow,
       reset_out;
  wire [3:0] control_1_alu_code, multiplexer_4_out, multiplexer_5_out, multiplexer_6_out, ram_1_data_2;
  wire [15:0] branch_val, immediate_1_output, main_1_output_1, main_1_output_2, multiplexer_1_out,
       multiplexer_2_out, multiplexer_7_out, multiplexer_8_out, multiplexer_9_out, n16_bit_alu_1_result,
       pc_t, ram_1_data, ram_2_data;

  Halt halt_1 (
    .instruction({ram_1_data[15:8], ram_1_data_2, ram_1_data[3:0]}), .clock(clock_1_out), .reset(reset_out),
    .halt(halt));
  Clock clock_1 (.out(clock_1_out));
  Button reset (.out(reset_out));
  and and_1 (and_1_out, ~halt, clock_1_out);  // AND_Gate
  and and_2 (and_2_out, and_1_out, ~n16_bit_alu_1_overflow);  // AND_Gate
  Multiplexer #(.width(16)) multiplexer_1 (
    .in0({16{1'b0}}), .in1(branch_val), .out(multiplexer_1_out), .sel(and_3_out));  // open: en
  Adder #(.width(16)) adder_1 (.a(multiplexer_1_out), .b(pc), .out(pc_t), .cin(1'b1));  // open: cout
  Multiplexer #(.width(16)) multiplexer_2 (
    .in0(pc_t), .in1(branch_val), .out(multiplexer_2_out), .sel(control_1_jump));  // open: en
  _16bit_register u_16bit_register_1 (
    .\input (multiplexer_2_out), .reset(reset_out), .write(1'b1), .Clock(and_2_out), .out_5(pc));
  RAM #(.addrWidth(16), .dataWidth(16), .bus("separate")) ram_1 (
    .addr(pc), .data({ram_1_data[15:8], ram_1_data_2, ram_1_data[3:0]}), .str(1'b0), .clk(and_2_out));  // open: din, sel, ld, clr
  Control control_1 (
    .in_1({ram_1_data[15:8], ram_1_data_2, ram_1_data[3:0]}), .RegDst(control_1_regdst),
    .RegWrite(control_1_regwrite), .ALUSrc(control_1_alusrc), .BranchRel(control_1_branchrel),
    .MemRead(control_1_memread), .MemWrite(control_1_memwrite), .MemToReg(control_1_memtoreg),
    .regAdress(control_1_regadress), .BranchImm(control_1_branchimm), .Jump(control_1_jump),
    .JAL(control_1_jal), .ALU_Code(control_1_alu_code));
  Immediate immediate_1 (.in_1({ram_1_data[15:8], ram_1_data_2, ram_1_data[3:0]}), .OUTPUT(immediate_1_output));
  Multiplexer #(.width(16)) multiplexer_3 (
    .in0(n16_bit_alu_1_result), .in1(immediate_1_output), .out(branch_val), .sel(control_1_branchimm));  // open: en
  Multiplexer #(.width(4)) multiplexer_4 (
    .in0(ram_1_data[3:0]), .in1(ram_1_data[11:8]), .out(multiplexer_4_out), .sel(control_1_regadress));  // open: en
  and and_3 (and_3_out, control_1_branchrel, ~n16_bit_alu_1_result[0]);  // AND_Gate
  Multiplexer #(.width(4)) multiplexer_5 (
    .in0(ram_1_data_2), .in1(ram_1_data[11:8]), .out(multiplexer_5_out), .sel(control_1_regdst));  // open: en
  Multiplexer #(.width(4)) multiplexer_6 (
    .in0(multiplexer_5_out), .in1(4'b1111), .out(multiplexer_6_out), .sel(control_1_jal));  // open: en
  modified_register_main main_1 (
    .Register_nummer(multiplexer_6_out), .Write_enable(control_1_regwrite), .Reset(reset_out),
    .value(multiplexer_7_out), .in_5(and_2_out), .r0(r0), .r1(r1), .r2(r2), .r3(r3), .r4(r4), .r5(r5),
    .r6(r6), .r7(r7), .r8(r8), .r9(r9), .r10(r10), .r11(r11), .r12(r12), .r13(r13), .r14(r14), .r15(r15),
    .output_1(main_1_output_1), .register_1(ram_1_data_2), .output_2(main_1_output_2),
    .register_2(multiplexer_4_out));
  Multiplexer #(.width(16)) multiplexer_7 (
    .in0(multiplexer_9_out), .in1(ram_2_data), .out(multiplexer_7_out), .sel(control_1_memtoreg));  // open: en
  Multiplexer #(.width(16)) multiplexer_8 (
    .in0(main_1_output_1), .in1(immediate_1_output), .out(multiplexer_8_out), .sel(control_1_alusrc));  // open: en
  Multiplexer #(.width(16)) multiplexer_9 (
    .in0(n16_bit_alu_1_result), .in1(pc_t), .out(multiplexer_9_out), .sel(control_1_jal));  // open: en
  _16_bit_ALU u_16_bit_alu_1 (
    .ALU_code(control_1_alu_code), .a(multiplexer_8_out), .b(main_1_output_2),
    .overflow(n16_bit_alu_1_overflow), .result(n16_bit_alu_1_result));
  RAM #(.addrWidth(16), .dataWidth(16), .bus("separate")) ram_2 (
    .addr(n16_bit_alu_1_result), .din(main_1_output_1), .data(ram_2_data), .str(control_1_memwrite),
    .clk(and_2_out), .ld(control_1_memread));  // open: sel, clr

  // Notes on the sheet:
  //   current instruction
  //   clock signal
  //   DO NOT CHANGE THE INPUTS AND OUTPUTS OF THIS CIRCUIT! Do not add/remove inputs or outputs. Do not even change their location or orientation.
endmodule

module Halt (
  input  [15:0] instruction,
  input  clock,
  input  reset,
  output halt
);

  wire and_1_out, comparator_1_eq, comparator_2_gt, counter_1_carry, or_1_out, or_2_out;
  wire [15:0] counter_1_q;

  Comparator #(.width(16), .mode("unsigned")) comparator_1 (
    .a(instruction), .b({16{1'b0}}), .eq(comparator_1_eq));  // open: gt, lt
  Counter #(.width(16), .max('hffff), .trigger("falling")) counter_1 (
    .Q(counter_1_q), .carry(counter_1_carry), .clk(clock), .clr(reset));  // open: load, D, count
  or or_1 (or_1_out, comparator_1_eq, counter_1_carry);
  Comparator #(.width(16), .mode("unsigned")) comparator_2 (
    .a(counter_1_q), .b({16{1'b0}}), .gt(comparator_2_gt));  // open: eq, lt
  or or_2 (or_2_out, halt, and_1_out);
  and and_1 (and_1_out, or_1_out, comparator_2_gt);
  Register #(.width(1)) register_1 (.D(or_2_out), .Q(halt), .clk(clock), .clr(reset));  // open: en

  // Notes on the sheet:
  //   halt becomes and stays asserted if the instruction is 0000 (not in the first clock cycle) or the end of the counter is reached (2^16)
endmodule

module _16_bit_register (
  input  in_1,
  input  write,
  input  reset,
  input  [15:0] in_4,
  output [15:0] out_5
);

  D_Flip_Flop #(.trigger("falling")) d_ff_1 (
    .clk(in_1), .D(in_4[0]), .Q(out_5[0]), .en(write), .reset(reset));  // open: Qn, preset
  D_Flip_Flop #(.trigger("falling")) d_ff_2 (
    .clk(in_1), .D(in_4[1]), .Q(out_5[1]), .en(write), .reset(reset));  // open: Qn, preset
  D_Flip_Flop #(.trigger("falling")) d_ff_3 (
    .clk(in_1), .D(in_4[2]), .Q(out_5[2]), .en(write), .reset(reset));  // open: Qn, preset
  D_Flip_Flop #(.trigger("falling")) d_ff_4 (
    .clk(in_1), .D(in_4[3]), .Q(out_5[3]), .en(write), .reset(reset));  // open: Qn, preset
  D_Flip_Flop #(.trigger("falling")) d_ff_5 (
    .clk(in_1), .D(in_4[4]), .Q(out_5[4]), .en(write), .reset(reset));  // open: Qn, preset
  D_Flip_Flop #(.trigger("falling")) d_ff_6 (
    .clk(in_1), .D(in_4[5]), .Q(out_5[5]), .en(write), .reset(reset));  // open: Qn, preset
  D_Flip_Flop #(.trigger("falling")) d_ff_7 (
    .clk(in_1), .D(in_4[6]), .Q(out_5[6]), .en(write), .reset(reset));  // open: Qn, preset
  D_Flip_Flop #(.trigger("falling")) d_ff_8 (
    .clk(in_1), .D(in_4[7]), .Q(out_5[7]), .en(write), .reset(reset));  // open: Qn, preset
  D_Flip_Flop #(.trigger("falling")) d_ff_9 (
    .clk(in_1), .D(in_4[8]), .Q(out_5[8]), .en(write), .reset(reset));  // open: Qn, preset
  D_Flip_Flop #(.trigger("falling")) d_ff_10 (
    .clk(in_1), .D(in_4[9]), .Q(out_5[9]), .en(write), .reset(reset));  // open: Qn, preset
  D_Flip_Flop #(.trigger("falling")) d_ff_11 (
    .clk(in_1), .D(in_4[10]), .Q(out_5[10]), .en(write), .reset(reset));  // open: Qn, preset
  D_Flip_Flop #(.trigger("falling")) d_ff_12 (
    .clk(in_1), .D(in_4[11]), .Q(out_5[11]), .en(write), .reset(reset));  // open: Qn, preset
  D_Flip_Flop #(.trigger("falling")) d_ff_13 (
    .clk(in_1), .D(in_4[12]), .Q(out_5[12]), .en(write), .reset(reset));  // open: Qn, preset
  D_Flip_Flop #(.trigger("falling")) d_ff_14 (
    .clk(in_1), .D(in_4[13]), .Q(out_5[13]), .en(write), .reset(reset));  // open: Qn, preset
  D_Flip_Flop #(.trigger("falling")) d_ff_15 (
    .clk(in_1), .D(in_4[14]), .Q(out_5[14]), .en(write), .reset(reset));  // open: Qn, preset
  D_Flip_Flop #(.trigger("falling")) d_ff_16 (
    .clk(in_1), .D(in_4[15]), .Q(out_5[15]), .en(write), .reset(reset));  // open: Qn, preset
endmodule

module Program_Counter (
  input  Branch_rel,
  input  Branch_abs,
  input  [15:0] Branch_val,
  input  Clock,
  input  reset,
  output [15:0] Output
);

  wire and_1_out, not_1_out, or_1_out;
  wire [15:0] adder_1_out, adder_2_out, bit_extender_1_out, multiplexer_1_out, multiplexer_2_out;

  and and_1 (and_1_out, ~Branch_rel, Branch_abs);  // AND_Gate
  Adder #(.width(16)) adder_1 (.a(Branch_val), .b(16'h1), .out(adder_1_out));  // open: cin, cout
  or or_1 (or_1_out, Branch_rel, and_1_out);
  not not_1 (not_1_out, or_1_out);
  assign bit_extender_1_out = {{15{1'b0}}, Clock};  // Bit_Extender bit_extender_1
  Multiplexer #(.width(16)) multiplexer_1 (
    .in0(adder_1_out), .in1(bit_extender_1_out), .out(multiplexer_1_out), .sel(not_1_out));  // open: en
  Adder #(.width(16)) adder_2 (.a(multiplexer_1_out), .b(Output), .out(adder_2_out));  // open: cin, cout
  Multiplexer #(.width(16)) multiplexer_2 (
    .in0(adder_2_out), .in1(Branch_val), .out(multiplexer_2_out), .sel(and_1_out));  // open: en
  _16_bit_register u_16_bit_register_1 (
    .in_4(multiplexer_2_out), .out_5(Output), .in_1(Clock), .reset(reset), .write(1'b1));
endmodule

module Immediate (
  input  [15:0] in_1,
  output [15:0] OUTPUT
);

  wire comparator_1_eq, comparator_2_eq, comparator_3_eq, comparator_4_eq, comparator_5_eq, comparator_6_eq,
       comparator_7_eq, comparator_8_eq;
  wire [15:0] and_1_out, and_2_out, and_3_out, and_4_out, and_5_out, and_6_out, and_7_out, and_8_out,
       bit_extender_1_out, bit_extender_2_out, bit_extender_3_out, bit_extender_4_out, bit_extender_5_out,
       bit_extender_6_out, bit_extender_7_out, bit_extender_8_out, bit_extender_9_out, bit_extender_10_out,
       bit_extender_11_out, bit_extender_12_out, bit_extender_13_out;

  assign bit_extender_1_out = {{12{1'b0}}, in_1[3:0]};  // Bit_Extender bit_extender_1
  Comparator #(.width(4)) comparator_1 (.a(4'b1000), .b(in_1[15:12]), .eq(comparator_1_eq));  // open: gt, lt
  Comparator #(.width(4)) comparator_2 (.a(4'b1001), .b(in_1[15:12]), .eq(comparator_2_eq));  // open: gt, lt
  Comparator #(.width(4)) comparator_3 (.a(4'b1010), .b(in_1[15:12]), .eq(comparator_3_eq));  // open: gt, lt
  assign bit_extender_2_out = {{8{1'b0}}, in_1[7:0]};  // Bit_Extender bit_extender_2
  Comparator #(.width(4)) comparator_4 (.a(4'b1011), .b(in_1[15:12]), .eq(comparator_4_eq));  // open: gt, lt
  Comparator #(.width(4)) comparator_5 (.a(4'b1100), .b(in_1[15:12]), .eq(comparator_5_eq));  // open: gt, lt
  Comparator #(.width(4)) comparator_6 (.a(4'b1101), .b(in_1[15:12]), .eq(comparator_6_eq));  // open: gt, lt
  Comparator #(.width(4)) comparator_7 (.a(4'b1110), .b(in_1[15:12]), .eq(comparator_7_eq));  // open: gt, lt
  Comparator #(.width(4)) comparator_8 (.a(4'b1111), .b(in_1[15:12]), .eq(comparator_8_eq));  // open: gt, lt
  assign bit_extender_3_out = {{15{comparator_1_eq}}, comparator_1_eq};  // Bit_Extender bit_extender_3
  assign bit_extender_4_out = {{15{comparator_2_eq}}, comparator_2_eq};  // Bit_Extender bit_extender_4
  assign bit_extender_5_out = {{15{comparator_3_eq}}, comparator_3_eq};  // Bit_Extender bit_extender_5
  assign bit_extender_6_out = {{15{comparator_4_eq}}, comparator_4_eq};  // Bit_Extender bit_extender_6
  assign bit_extender_7_out = {{15{comparator_5_eq}}, comparator_5_eq};  // Bit_Extender bit_extender_7
  assign bit_extender_8_out = {{12{in_1[3]}}, in_1[3:0]};  // Bit_Extender bit_extender_8
  assign bit_extender_9_out = {{15{comparator_6_eq}}, comparator_6_eq};  // Bit_Extender bit_extender_9
  assign bit_extender_10_out = {{4{1'b0}}, in_1[11:0]};  // Bit_Extender bit_extender_10
  assign bit_extender_11_out = {{15{comparator_7_eq}}, comparator_7_eq};  // Bit_Extender bit_extender_11
  assign bit_extender_12_out = {{8{in_1[7]}}, in_1[7:0]};  // Bit_Extender bit_extender_12
  assign bit_extender_13_out = {{15{comparator_8_eq}}, comparator_8_eq};  // Bit_Extender bit_extender_13
  assign and_1_out = bit_extender_1_out & bit_extender_3_out;  // AND_Gate and_1, 16 bits wide
  assign and_2_out = bit_extender_1_out & bit_extender_4_out;  // AND_Gate and_2, 16 bits wide
  assign and_3_out = bit_extender_5_out & bit_extender_2_out;  // AND_Gate and_3, 16 bits wide
  assign and_4_out = bit_extender_2_out & bit_extender_6_out;  // AND_Gate and_4, 16 bits wide
  assign and_5_out = {in_1[7:0], {8{1'b0}}} & bit_extender_7_out;  // AND_Gate and_5, 16 bits wide
  assign and_6_out = bit_extender_8_out & bit_extender_9_out;  // AND_Gate and_6, 16 bits wide
  assign and_7_out = bit_extender_10_out & bit_extender_11_out;  // AND_Gate and_7, 16 bits wide
  assign and_8_out = bit_extender_12_out & bit_extender_13_out;  // AND_Gate and_8, 16 bits wide
  assign OUTPUT = and_1_out | and_2_out | and_3_out | and_4_out | and_5_out | and_6_out | and_7_out | and_8_out;  // OR_Gate or_1, 16 bits wide

  // Notes on the sheet:
  //   JAL nog toevoegen
endmodule

module Control (
  input  [15:0] in_1,
  output RegDst,
  output RegWrite,
  output ALUSrc,
  output BranchRel,
  output Jump,
  output MemRead,
  output MemWrite,
  output MemToReg,
  output regAdress,
  output BranchImm,
  output JAL,
  output [3:0] ALU_Code
);

  wire comparator_1_eq, comparator_2_eq, comparator_3_eq, comparator_4_eq, comparator_5_gt, comparator_6_eq,
       comparator_13_eq, not_2_out;
  wire [3:0] adder_1_out;

  Comparator #(.width(4), .mode("unsigned")) comparator_1 (
    .a(in_1[15:12]), .b(4'b1000), .eq(comparator_1_eq));  // open: gt, lt
  Comparator #(.width(4), .mode("unsigned")) comparator_2 (
    .a(in_1[15:12]), .b(4'b1001), .eq(comparator_2_eq));  // open: gt, lt
  Comparator #(.width(4), .mode("unsigned")) comparator_3 (
    .a(in_1[15:12]), .b(4'b1101), .eq(comparator_3_eq));  // open: gt, lt
  Comparator #(.width(4), .mode("unsigned")) comparator_4 (
    .a(in_1[15:12]), .b(4'b1111), .eq(comparator_4_eq));  // open: gt, lt
  Comparator #(.width(4), .mode("unsigned")) comparator_5 (
    .a(in_1[15:12]), .b(4'b0111), .gt(comparator_5_gt));  // open: eq, lt
  Comparator #(.width(4), .mode("unsigned")) comparator_6 (
    .a(in_1[15:12]), .b(4'b1101), .eq(comparator_6_eq));  // open: gt, lt
  Comparator #(.width(4), .mode("unsigned")) comparator_7 (
    .a(in_1[15:12]), .b(4'b1101), .eq(BranchRel));  // open: gt, lt
  Comparator #(.width(4), .mode("unsigned")) comparator_8 (.a(in_1[15:12]), .b(4'b1101), .gt(Jump));  // open: eq, lt
  Comparator #(.width(4), .mode("unsigned")) comparator_9 (.a(in_1[15:12]), .b(4'b1000), .eq(MemRead));  // open: gt, lt
  Comparator #(.width(4), .mode("unsigned")) comparator_10 (
    .a(in_1[15:12]), .b(4'b1001), .eq(MemWrite));  // open: gt, lt
  Comparator #(.width(4), .mode("unsigned")) comparator_11 (
    .a(in_1[15:12]), .b(4'b1000), .eq(MemToReg));  // open: gt, lt
  Comparator #(.width(4), .mode("unsigned")) comparator_12 (
    .a(in_1[15:12]), .b(4'b0110), .gt(regAdress));  // open: eq, lt
  Comparator #(.width(4), .mode("unsigned")) comparator_13 (
    .a(in_1[15:12]), .b(4'b1111), .eq(comparator_13_eq));  // open: gt, lt
  Comparator #(.width(4), .mode("unsigned")) comparator_14 (.a(in_1[15:12]), .b(4'b1110), .eq(JAL));  // open: gt, lt
  Adder #(.width(4)) adder_1 (.a(in_1[15:12]), .b(in_1[3:0]), .out(adder_1_out));  // open: cin, cout
  not not_1 (RegDst, comparator_1_eq);
  nor nor_1 (RegWrite, comparator_2_eq, comparator_3_eq, comparator_4_eq);
  not not_2 (not_2_out, comparator_6_eq);
  not not_3 (BranchImm, comparator_13_eq);
  and and_1 (ALUSrc, comparator_5_gt, not_2_out);
  Multiplexer #(.select(4), .width(4)) multiplexer_1 (
    .in0(in_1[15:12]), .in1(in_1[15:12]), .in2(in_1[15:12]), .in3(in_1[15:12]), .in4(in_1[15:12]),
    .in5(in_1[15:12]), .in6(in_1[15:12]), .in7(adder_1_out), .in8(4'b0010), .in9(4'b0010), .in10(4'b0010),
    .in11(4'b0000), .in12(4'b0010), .in13(4'b0110), .in14(4'b0111), .in15(4'b0010), .out(ALU_Code),
    .sel(in_1[15:12]));  // open: en

  // Notes on the sheet:
  //   (8-11) = register to write to if False, if true, write to (4-7)
  //   Only False with Sw, Bne, Jr
  //   True: load something from memory
  //   True: Write something to memory
  //   True: write Mem to reg, False: Write ALU data to reg
  //   true: load 2nd adress from 8-11 ipv 0-3
  //   Use the second register as second operand or use an immediate as second operand
  //   True: Use an input for the PC, False use the default PC+1
  //   True: use immediate to jump, false: use ALU input to jump
endmodule

module test1 (
  input  Clock,
  output [15:0] r0,
  output [15:0] r1,
  output [15:0] r2,
  output [15:0] r3,
  output [15:0] r4,
  output [15:0] r5,
  output [15:0] r6,
  output [15:0] r7,
  output [15:0] r8,
  output [15:0] r9,
  output [15:0] r10,
  output [15:0] r11,
  output [15:0] r12,
  output [15:0] r13,
  output [15:0] r14,
  output [15:0] r15
);

  wire and_1_out, control_1_alusrc, control_1_branchimm, control_1_branchrel, control_1_jal, control_1_jump,
       control_1_memread, control_1_memtoreg, control_1_memwrite, control_1_regadress, control_1_regdst,
       control_1_regwrite, undriven;
  wire [3:0] control_1_alu_code, multiplexer_4_out, multiplexer_5_out, multiplexer_6_out;
  wire [15:0] branch_val, immediate_1_output, main_1_output_1, main_1_output_2, multiplexer_1_out,
       multiplexer_2_out, multiplexer_7_out, multiplexer_8_out, multiplexer_9_out, multiplexer_10_out,
       n16_bit_alu_1_result, n16bit_register_1_out_5, pc, ram_1_data, ram_2_data;

  Multiplexer #(.width(16)) multiplexer_1 (
    .in0({16{1'b0}}), .in1(branch_val), .out(multiplexer_1_out), .sel(and_1_out));  // open: en
  Adder #(.width(16)) adder_1 (.a(multiplexer_1_out), .b(n16bit_register_1_out_5), .out(pc), .cin(1'b1));  // open: cout
  Multiplexer #(.width(16)) multiplexer_2 (
    .in0(pc), .in1(branch_val), .out(multiplexer_2_out), .sel(control_1_jump));  // open: en
  _16bit_register u_16bit_register_1 (
    .\input (multiplexer_2_out), .write(1'b1), .Clock(Clock), .out_5(n16bit_register_1_out_5));  // open: reset
  RAM #(.addrWidth(16), .dataWidth(16), .bus("separate")) ram_1 (
    .addr(n16bit_register_1_out_5), .data(ram_1_data), .str(1'b0), .clk(Clock));  // open: din, sel, ld, clr
  Control control_1 (
    .in_1(ram_1_data), .RegDst(control_1_regdst), .RegWrite(control_1_regwrite), .ALUSrc(control_1_alusrc),
    .BranchRel(control_1_branchrel), .MemRead(control_1_memread), .MemWrite(control_1_memwrite),
    .MemToReg(control_1_memtoreg), .regAdress(control_1_regadress), .BranchImm(control_1_branchimm),
    .Jump(control_1_jump), .JAL(control_1_jal), .ALU_Code(control_1_alu_code));
  Immediate immediate_1 (.in_1(ram_1_data), .OUTPUT(immediate_1_output));
  Multiplexer #(.width(16)) multiplexer_3 (
    .in0(n16_bit_alu_1_result), .in1(immediate_1_output), .out(branch_val), .sel(control_1_branchimm));  // open: en
  Multiplexer #(.width(4)) multiplexer_4 (
    .in0(ram_1_data[7:4]), .in1(ram_1_data[11:8]), .out(multiplexer_4_out), .sel(control_1_regdst));  // open: en
  Multiplexer #(.width(4)) multiplexer_5 (
    .in0(ram_1_data[3:0]), .in1(ram_1_data[11:8]), .out(multiplexer_5_out), .sel(control_1_regadress));  // open: en
  and and_1 (and_1_out, control_1_branchrel, ~n16_bit_alu_1_result[0]);  // AND_Gate
  Multiplexer #(.width(4)) multiplexer_6 (
    .in0(multiplexer_4_out), .in1(4'b1111), .out(multiplexer_6_out), .sel(control_1_jal));  // open: en
  modified_register_main main_1 (
    .Register_nummer(multiplexer_6_out), .Write_enable(control_1_regwrite), .value(multiplexer_7_out),
    .in_5(Clock), .r0(r0), .r1(r1), .r2(r2), .r3(r3), .r4(r4), .r5(r5), .r6(r6), .r7(r7), .r8(r8), .r9(r9),
    .r10(r10), .r11(r11), .r12(r12), .r13(r13), .r14(r14), .r15(r15), .output_1(main_1_output_1),
    .register_1(ram_1_data[7:4]), .output_2(main_1_output_2), .register_2(multiplexer_5_out));  // open: Reset
  Multiplexer #(.width(16)) multiplexer_7 (
    .in0(n16_bit_alu_1_result), .in1(multiplexer_10_out), .out(multiplexer_7_out), .sel(control_1_memtoreg));  // open: en
  Multiplexer #(.width(16)) multiplexer_8 (
    .in0(main_1_output_2), .in1(immediate_1_output), .out(multiplexer_8_out), .sel(control_1_alusrc));  // open: en
  Multiplexer #(.width(16)) multiplexer_9 (
    .in0(main_1_output_1), .in1({16{1'b0}}), .out(multiplexer_9_out), .sel(undriven));  // open: en
  _16_bit_ALU u_16_bit_alu_1 (
    .ALU_code(control_1_alu_code), .a(multiplexer_9_out), .b(multiplexer_8_out), .result(n16_bit_alu_1_result));  // open: overflow
  Multiplexer #(.width(16)) multiplexer_10 (
    .in0(ram_2_data), .in1(pc), .out(multiplexer_10_out), .sel(control_1_memtoreg));  // open: en
  RAM #(.addrWidth(16), .dataWidth(16), .bus("separate")) ram_2 (
    .addr(n16_bit_alu_1_result), .din(main_1_output_2), .data(ram_2_data), .str(control_1_memwrite),
    .clk(Clock), .ld(control_1_memread));  // open: sel, clr
endmodule
