// Logisim project Sessie4Oefening2.circ as structural Verilog: 4 circuits, main circuit main
module main (
  input  [3:0] register_1,
  input  [3:0] Register_nummer,
  input  Write_enable,
  input  Reset,
  input  [3:0] register_2,
  input  [15:0] in_6,
  input  in_7,
  output [15:0] output_1,
  output [15:0] Output_2
);

  wire and_1_out, and_2_out, and_3_out, and_4_out, and_5_out, and_6_out, and_7_out, and_8_out, and_9_out,
       and_10_out, and_11_out, and_12_out, and_13_out, and_14_out, and_15_out, decoder_1_out_3,
       decoder_1_out_4, decoder_1_out_5, decoder_1_out_6, decoder_1_out_7, decoder_1_out_8, decoder_1_out_9,
       decoder_1_out_10, decoder_1_out_11, decoder_1_out_12, decoder_1_out_13, decoder_1_out_14,
       decoder_1_out_15, decoder_1_out_16, decoder_1_out_17;
  wire [15:0] n16bit_register_1_out_5, n16bit_register_2_out_5, n16bit_register_3_out_5,
       n16bit_register_4_out_5, n16bit_register_5_out_5, n16bit_register_6_out_5, n16bit_register_7_out_5,
       n16bit_register_8_out_5, n16bit_register_9_out_5, n16bit_register_10_out_5, n16bit_register_11_out_5,
       n16bit_register_12_out_5, n16bit_register_13_out_5, n16bit_register_14_out_5,
       n16bit_register_15_out_5, n16bit_register_16_out_5;

  Decoder decoder_1 (
    .in_1(Register_nummer), .out_3(decoder_1_out_3), .out_4(decoder_1_out_4), .out_5(decoder_1_out_5),
    .out_6(decoder_1_out_6), .out_7(decoder_1_out_7), .out_8(decoder_1_out_8), .out_9(decoder_1_out_9),
    .out_10(decoder_1_out_10), .out_11(decoder_1_out_11), .out_12(decoder_1_out_12),
    .out_13(decoder_1_out_13), .out_14(decoder_1_out_14), .out_15(decoder_1_out_15),
    .out_16(decoder_1_out_16), .out_17(decoder_1_out_17));  // open: out_2
  _16bit_register u_16bit_register_1 (
    .\input (in_6), .reset(Reset), .write(1'b0), .Clock(in_7), .out_5(n16bit_register_1_out_5));
  and and_1 (and_1_out, decoder_1_out_3, Write_enable);
  _16bit_register u_16bit_register_2 (
    .\input (in_6), .reset(Reset), .write(and_1_out), .Clock(in_7), .out_5(n16bit_register_2_out_5));
  and and_2 (and_2_out, decoder_1_out_4, Write_enable);
  _16bit_register u_16bit_register_3 (
    .\input (in_6), .reset(Reset), .write(and_2_out), .Clock(in_7), .out_5(n16bit_register_3_out_5));
  and and_3 (and_3_out, decoder_1_out_5, Write_enable);
  _16bit_register u_16bit_register_4 (
    .\input (in_6), .reset(Reset), .write(and_3_out), .Clock(in_7), .out_5(n16bit_register_4_out_5));
  and and_4 (and_4_out, decoder_1_out_6, Write_enable);
  _16bit_register u_16bit_register_5 (
    .\input (in_6), .reset(Reset), .write(and_4_out), .Clock(in_7), .out_5(n16bit_register_5_out_5));
  and and_5 (and_5_out, decoder_1_out_7, Write_enable);
  _16bit_register u_16bit_register_6 (
    .\input (in_6), .reset(Reset), .write(and_5_out), .Clock(in_7), .out_5(n16bit_register_6_out_5));
  and and_6 (and_6_out, decoder_1_out_8, Write_enable);
  _16bit_register u_16bit_register_7 (
    .\input (in_6), .reset(Reset), .write(and_6_out), .Clock(in_7), .out_5(n16bit_register_7_out_5));
  and and_7 (and_7_out, decoder_1_out_9, Write_enable);
  _16bit_register u_16bit_register_8 (
    .\input (in_6), .reset(Reset), .write(and_7_out), .Clock(in_7), .out_5(n16bit_register_8_out_5));
  and and_8 (and_8_out, decoder_1_out_10, Write_enable);
  _16bit_register u_16bit_register_9 (
    .\input (in_6), .reset(Write_enable), .write(and_8_out), .Clock(in_7), .out_5(n16bit_register_9_out_5));
  and and_9 (and_9_out, decoder_1_out_11, Write_enable);
  _16bit_register u_16bit_register_10 (
    .\input (in_6), .reset(Reset), .write(and_9_out), .Clock(in_7), .out_5(n16bit_register_10_out_5));
  and and_10 (and_10_out, decoder_1_out_12, Write_enable);
  _16bit_register u_16bit_register_11 (
    .\input (in_6), .reset(Reset), .write(and_10_out), .Clock(in_7), .out_5(n16bit_register_11_out_5));
  and and_11 (and_11_out, decoder_1_out_13, Write_enable);
  _16bit_register u_16bit_register_12 (
    .\input (in_6), .reset(Reset), .write(and_11_out), .Clock(in_7), .out_5(n16bit_register_12_out_5));
  and and_12 (and_12_out, decoder_1_out_14, Write_enable);
  _16bit_register u_16bit_register_13 (
    .\input (in_6), .reset(Reset), .write(and_12_out), .Clock(in_7), .out_5(n16bit_register_13_out_5));
  and and_13 (and_13_out, decoder_1_out_15, Write_enable);
  _16bit_register u_16bit_register_14 (
    .\input (in_6), .reset(Reset), .write(and_13_out), .Clock(in_7), .out_5(n16bit_register_14_out_5));
  and and_14 (and_14_out, decoder_1_out_16, Write_enable);
  _16bit_register u_16bit_register_15 (
    .\input (in_6), .reset(Reset), .write(and_14_out), .Clock(in_7), .out_5(n16bit_register_15_out_5));
  and and_15 (and_15_out, decoder_1_out_17, Write_enable);
  _16bit_register u_16bit_register_16 (
    .\input (in_6), .reset(Reset), .write(and_15_out), .Clock(in_7), .out_5(n16bit_register_16_out_5));
  Multiplexer #(.select(4), .width(16)) multiplexer_1 (
    .in0(n16bit_register_1_out_5), .in1(n16bit_register_2_out_5), .in2(n16bit_register_3_out_5),
    .in3(n16bit_register_4_out_5), .in4(n16bit_register_5_out_5), .in5(n16bit_register_6_out_5),
    .in6(n16bit_register_7_out_5), .in7(n16bit_register_8_out_5), .in8(n16bit_register_9_out_5),
    .in9(n16bit_register_10_out_5), .in10(n16bit_register_11_out_5), .in11(n16bit_register_12_out_5),
    .in12(n16bit_register_13_out_5), .in13(n16bit_register_14_out_5), .in14(n16bit_register_15_out_5),
    .in15(n16bit_register_16_out_5), .out(output_1), .sel(register_1));  // open: en
  Multiplexer #(.select(4), .width(16)) multiplexer_2 (
    .in0(n16bit_register_1_out_5), .in1(n16bit_register_2_out_5), .in2(n16bit_register_3_out_5),
    .in3(n16bit_register_4_out_5), .in4(n16bit_register_5_out_5), .in5(n16bit_register_6_out_5),
    .in6(n16bit_register_7_out_5), .in7(n16bit_register_8_out_5), .in8(n16bit_register_9_out_5),
    .in9(n16bit_register_10_out_5), .in10(n16bit_register_11_out_5), .in11(n16bit_register_12_out_5),
    .in12(n16bit_register_13_out_5), .in13(n16bit_register_14_out_5), .in14(n16bit_register_15_out_5),
    .in15(n16bit_register_16_out_5), .out(Output_2), .sel(register_2));  // open: en
endmodule

module _16bit_register (
  input  Clock,
  input  write,
  input  reset,
  input  [15:0] \input ,
  output [15:0] out_5
);

  D_Flip_Flop #(.trigger("falling")) d_ff_1 (
    .clk(Clock), .D(\input [0]), .Q(out_5[0]), .en(write), .reset(reset));  // open: Qn, preset
  D_Flip_Flop #(.trigger("falling")) d_ff_2 (
    .clk(Clock), .D(\input [1]), .Q(out_5[1]), .en(write), .reset(reset));  // open: Qn, preset
  D_Flip_Flop #(.trigger("falling")) d_ff_3 (
    .clk(Clock), .D(\input [2]), .Q(out_5[2]), .en(write), .reset(reset));  // open: Qn, preset
  D_Flip_Flop #(.trigger("falling")) d_ff_4 (
    .clk(Clock), .D(\input [3]), .Q(out_5[3]), .en(write), .reset(reset));  // open: Qn, preset
  D_Flip_Flop #(.trigger("falling")) d_ff_5 (
    .clk(Clock), .D(\input [4]), .Q(out_5[4]), .en(write), .reset(reset));  // open: Qn, preset
  D_Flip_Flop #(.trigger("falling")) d_ff_6 (
    .clk(Clock), .D(\input [5]), .Q(out_5[5]), .en(write), .reset(reset));  // open: Qn, preset
  D_Flip_Flop #(.trigger("falling")) d_ff_7 (
    .clk(Clock), .D(\input [6]), .Q(out_5[6]), .en(write), .reset(reset));  // open: Qn, preset
  D_Flip_Flop #(.trigger("falling")) d_ff_8 (
    .clk(Clock), .D(\input [7]), .Q(out_5[7]), .en(write), .reset(reset));  // open: Qn, preset
  D_Flip_Flop #(.trigger("falling")) d_ff_9 (
    .clk(Clock), .D(\input [8]), .Q(out_5[8]), .en(write), .reset(reset));  // open: Qn, preset
  D_Flip_Flop #(.trigger("falling")) d_ff_10 (
    .clk(Clock), .D(\input [9]), .Q(out_5[9]), .en(write), .reset(reset));  // open: Qn, preset
  D_Flip_Flop #(.trigger("falling")) d_ff_11 (
    .clk(Clock), .D(\input [10]), .Q(out_5[10]), .en(write), .reset(reset));  // open: Qn, preset
  D_Flip_Flop #(.trigger("falling")) d_ff_12 (
    .clk(Clock), .D(\input [11]), .Q(out_5[11]), .en(write), .reset(reset));  // open: Qn, preset
  D_Flip_Flop #(.trigger("falling")) d_ff_13 (
    .clk(Clock), .D(\input [12]), .Q(out_5[12]), .en(write), .reset(reset));  // open: Qn, preset
  D_Flip_Flop #(.trigger("falling")) d_ff_14 (
    .clk(Clock), .D(\input [13]), .Q(out_5[13]), .en(write), .reset(reset));  // open: Qn, preset
  D_Flip_Flop #(.trigger("falling")) d_ff_15 (
    .clk(Clock), .D(\input [14]), .Q(out_5[14]), .en(write), .reset(reset));  // open: Qn, preset
  D_Flip_Flop #(.trigger("falling")) d_ff_16 (
    .clk(Clock), .D(\input [15]), .Q(out_5[15]), .en(write), .reset(reset));  // open: Qn, preset
endmodule

module Decoder (
  input  [3:0] in_1,
  output out_2,
  output out_3,
  output out_4,
  output out_5,
  output out_6,
  output out_7,
  output out_8,
  output out_9,
  output out_10,
  output out_11,
  output out_12,
  output out_13,
  output out_14,
  output out_15,
  output out_16,
  output out_17
);

  and _0 (out_2, ~in_1[0], ~in_1[1], ~in_1[2], ~in_1[3]);  // AND_Gate
  and _1 (out_3, in_1[0], ~in_1[1], ~in_1[2], ~in_1[3]);  // AND_Gate
  and _2 (out_4, ~in_1[0], in_1[1], ~in_1[2], ~in_1[3]);  // AND_Gate
  and _3 (out_5, in_1[0], in_1[1], ~in_1[2], ~in_1[3]);  // AND_Gate
  and _4 (out_6, ~in_1[0], ~in_1[1], in_1[2], ~in_1[3]);  // AND_Gate
  and _5 (out_7, in_1[0], ~in_1[1], in_1[2], ~in_1[3]);  // AND_Gate
  and _6 (out_8, ~in_1[0], in_1[1], in_1[2], ~in_1[3]);  // AND_Gate
  and _7 (out_9, in_1[0], in_1[1], in_1[2], ~in_1[3]);  // AND_Gate
  and _15 (out_17, in_1[0], in_1[1], in_1[2], in_1[3]);
  and _14 (out_16, ~in_1[0], in_1[1], in_1[2], in_1[3]);  // AND_Gate
  and _13 (out_15, in_1[0], ~in_1[1], in_1[2], in_1[3]);  // AND_Gate
  and _12 (out_14, ~in_1[0], ~in_1[1], in_1[2], in_1[3]);  // AND_Gate
  and _11 (out_13, in_1[0], in_1[1], ~in_1[2], in_1[3]);  // AND_Gate
  and _10 (out_12, ~in_1[0], in_1[1], ~in_1[2], in_1[3]);  // AND_Gate
  and _9 (out_11, in_1[0], ~in_1[1], ~in_1[2], in_1[3]);  // AND_Gate
  and _8 (out_10, ~in_1[0], ~in_1[1], ~in_1[2], in_1[3]);  // AND_Gate
endmodule

module test (
  input  [3:0] register_1,
  input  [3:0] Register_nummer,
  input  Write_enable,
  input  Reset,
  input  [3:0] register_2,
  input  [15:0] in_6,
  input  in_7,
  output [15:0] output_1,
  output [15:0] Output_2
);

  wire and_1_out, and_2_out, and_3_out, and_4_out, and_5_out, and_6_out, and_7_out, and_8_out, and_9_out,
       and_10_out, and_11_out, and_12_out, and_13_out, and_14_out, and_15_out, decoder_1_out_3,
       decoder_1_out_4, decoder_1_out_5, decoder_1_out_6, decoder_1_out_7, decoder_1_out_8, decoder_1_out_9,
       decoder_1_out_10, decoder_1_out_11, decoder_1_out_12, decoder_1_out_13, decoder_1_out_14,
       decoder_1_out_15, decoder_1_out_16, decoder_1_out_17;
  wire [15:0] n16bit_register_1_out_5, n16bit_register_2_out_5, n16bit_register_3_out_5,
       n16bit_register_4_out_5, n16bit_register_5_out_5, n16bit_register_6_out_5, n16bit_register_7_out_5,
       n16bit_register_8_out_5, n16bit_register_9_out_5, n16bit_register_10_out_5, n16bit_register_11_out_5,
       n16bit_register_12_out_5, n16bit_register_13_out_5, n16bit_register_14_out_5,
       n16bit_register_15_out_5, n16bit_register_16_out_5;

  Decoder decoder_1 (
    .in_1(Register_nummer), .out_3(decoder_1_out_3), .out_4(decoder_1_out_4), .out_5(decoder_1_out_5),
    .out_6(decoder_1_out_6), .out_7(decoder_1_out_7), .out_8(decoder_1_out_8), .out_9(decoder_1_out_9),
    .out_10(decoder_1_out_10), .out_11(decoder_1_out_11), .out_12(decoder_1_out_12),
    .out_13(decoder_1_out_13), .out_14(decoder_1_out_14), .out_15(decoder_1_out_15),
    .out_16(decoder_1_out_16), .out_17(decoder_1_out_17));  // open: out_2
  _16bit_register u_16bit_register_1 (
    .\input (in_6), .reset(Reset), .write(1'b0), .Clock(in_7), .out_5(n16bit_register_1_out_5));
  and and_1 (and_1_out, decoder_1_out_3, Write_enable);
  _16bit_register u_16bit_register_2 (
    .\input (in_6), .reset(Reset), .write(and_1_out), .Clock(in_7), .out_5(n16bit_register_2_out_5));
  and and_2 (and_2_out, decoder_1_out_4, Write_enable);
  _16bit_register u_16bit_register_3 (
    .\input (in_6), .reset(Reset), .write(and_2_out), .Clock(in_7), .out_5(n16bit_register_3_out_5));
  and and_3 (and_3_out, decoder_1_out_5, Write_enable);
  _16bit_register u_16bit_register_4 (
    .\input (in_6), .reset(Reset), .write(and_3_out), .Clock(in_7), .out_5(n16bit_register_4_out_5));
  and and_4 (and_4_out, decoder_1_out_6, Write_enable);
  _16bit_register u_16bit_register_5 (
    .\input (in_6), .reset(Reset), .write(and_4_out), .Clock(in_7), .out_5(n16bit_register_5_out_5));
  and and_5 (and_5_out, decoder_1_out_7, Write_enable);
  _16bit_register u_16bit_register_6 (
    .\input (in_6), .reset(Reset), .write(and_5_out), .Clock(in_7), .out_5(n16bit_register_6_out_5));
  and and_6 (and_6_out, decoder_1_out_8, Write_enable);
  _16bit_register u_16bit_register_7 (
    .\input (in_6), .reset(Reset), .write(and_6_out), .Clock(in_7), .out_5(n16bit_register_7_out_5));
  and and_7 (and_7_out, decoder_1_out_9, Write_enable);
  _16bit_register u_16bit_register_8 (
    .\input (in_6), .reset(Reset), .write(and_7_out), .Clock(in_7), .out_5(n16bit_register_8_out_5));
  and and_8 (and_8_out, decoder_1_out_10, Write_enable);
  _16bit_register u_16bit_register_9 (
    .\input (in_6), .reset(Write_enable), .write(and_8_out), .Clock(in_7), .out_5(n16bit_register_9_out_5));
  and and_9 (and_9_out, decoder_1_out_11, Write_enable);
  _16bit_register u_16bit_register_10 (
    .\input (in_6), .reset(Reset), .write(and_9_out), .Clock(in_7), .out_5(n16bit_register_10_out_5));
  and and_10 (and_10_out, decoder_1_out_12, Write_enable);
  _16bit_register u_16bit_register_11 (
    .\input (in_6), .reset(Reset), .write(and_10_out), .Clock(in_7), .out_5(n16bit_register_11_out_5));
  and and_11 (and_11_out, decoder_1_out_13, Write_enable);
  _16bit_register u_16bit_register_12 (
    .\input (in_6), .reset(Reset), .write(and_11_out), .Clock(in_7), .out_5(n16bit_register_12_out_5));
  and and_12 (and_12_out, decoder_1_out_14, Write_enable);
  _16bit_register u_16bit_register_13 (
    .\input (in_6), .reset(Reset), .write(and_12_out), .Clock(in_7), .out_5(n16bit_register_13_out_5));
  and and_13 (and_13_out, decoder_1_out_15, Write_enable);
  _16bit_register u_16bit_register_14 (
    .\input (in_6), .reset(Reset), .write(and_13_out), .Clock(in_7), .out_5(n16bit_register_14_out_5));
  and and_14 (and_14_out, decoder_1_out_16, Write_enable);
  _16bit_register u_16bit_register_15 (
    .\input (in_6), .reset(Reset), .write(and_14_out), .Clock(in_7), .out_5(n16bit_register_15_out_5));
  and and_15 (and_15_out, decoder_1_out_17, Write_enable);
  _16bit_register u_16bit_register_16 (
    .\input (in_6), .reset(Reset), .write(and_15_out), .Clock(in_7), .out_5(n16bit_register_16_out_5));
  Multiplexer #(.select(4), .width(16)) multiplexer_1 (
    .in0(n16bit_register_1_out_5), .in1(n16bit_register_2_out_5), .in2(n16bit_register_3_out_5),
    .in3(n16bit_register_4_out_5), .in4(n16bit_register_5_out_5), .in5(n16bit_register_6_out_5),
    .in6(n16bit_register_7_out_5), .in7(n16bit_register_8_out_5), .in8(n16bit_register_9_out_5),
    .in9(n16bit_register_10_out_5), .in10(n16bit_register_11_out_5), .in11(n16bit_register_12_out_5),
    .in12(n16bit_register_13_out_5), .in13(n16bit_register_14_out_5), .in14(n16bit_register_15_out_5),
    .in15(n16bit_register_16_out_5), .out(output_1), .sel(register_1));  // open: en
  Multiplexer #(.select(4), .width(16)) multiplexer_2 (
    .in0(n16bit_register_1_out_5), .in1(n16bit_register_2_out_5), .in2(n16bit_register_3_out_5),
    .in3(n16bit_register_4_out_5), .in4(n16bit_register_5_out_5), .in5(n16bit_register_6_out_5),
    .in6(n16bit_register_7_out_5), .in7(n16bit_register_8_out_5), .in8(n16bit_register_9_out_5),
    .in9(n16bit_register_10_out_5), .in10(n16bit_register_11_out_5), .in11(n16bit_register_12_out_5),
    .in12(n16bit_register_13_out_5), .in13(n16bit_register_14_out_5), .in14(n16bit_register_15_out_5),
    .in15(n16bit_register_16_out_5), .out(Output_2), .sel(register_2));  // open: en
endmodule
