// Logisim project subCircuitPorts.circ as structural Verilog
module SubCircuit (
  input  in_1,
  input  in_2,
  input  in_3,
  input  in_4,
  output out_5,
  output out_6,
  output out_7,
  output out_8
);
endmodule
