// Logisim project Oefening 4.circ as structural Verilog: 1 circuit, main circuit main
module main (
  input  INPUT_A,
  input  INPUT_B,
  input  INPUT_C,
  output OUTPUT_X,
  output OUTPUT_Y
);

  or or_1 (OUTPUT_X, INPUT_A, INPUT_B);
  and and_1 (OUTPUT_Y, OUTPUT_X, INPUT_C);
endmodule
