// Logisim project test.circ as structural Verilog: 3 circuits, main circuit main
module main (
  input  in_1,
  input  in_2,
  input  in_3,
  input  in_4,
  input  in_5,
  input  in_6,
  input  in_7,
  input  in_8,
  input  in_9,
  input  in_10,
  input  in_11,
  input  in_12,
  input  in_13,
  input  in_14,
  input  in_15,
  output out_16,
  output out_17,
  output out_18
);

  wire not_3_out, not_4_out;

  not not_1 (out_16, in_1);
  // AND_Gate and_1 has open pins: in0=in_3, in1=in_5, out=open
  // AND_Gate and_2 has open pins: in0=in_6, in1=in_7, out=open
  // AND_Gate and_3 has open pins: in0=in_8, in1=in_10, out=open
  // AND_Gate and_4 has open pins: in0=not_3_out, in1=in_14, out=open
  not not_2 (out_17, in_2);
  // AND_Gate and_5 has open pins: in0=in_4, in1=in_9, out=open
  not not_3 (not_3_out, in_11);
  // AND_Gate and_6 has open pins: in0=in_13, in1=not_4_out, out=open
  not not_4 (not_4_out, in_15);

  assign out_18 = in_12;
endmodule

module test (
  input  c,
  output out_2,
  output out_3
);


  assign out_2 = c;
  assign out_3 = c;
endmodule

module Pin (
  input  in_1,
  input  in_2
);

  // AND_Gate and_1 has open pins: in0=in_1, in1=in_2, out=open
endmodule
