// Logisim project Group03.circ as structural Verilog: 5 circuits, main circuit 1bit full-adder
module _1bit_full_adder (
  input  in_1,
  input  A,
  input  B,
  output Sum,
  output carry_out
);

  wire and_1_out, xor_1_out, xor_2_out;

  ExactlyOne xor_1 (.out(xor_1_out), .in1(A), .in2(B), .in3(in_1));
  and and_1 (and_1_out, A, B, in_1);
  ExactlyOne xor_2 (.out(xor_2_out), .in1(A), .in2(B), .in3(in_1));
  or or_1 (carry_out, xor_2_out, and_1_out);
  or or_2 (Sum, xor_1_out, and_1_out);

  // Notes on the sheet:
  //   carry-in
endmodule

module _4_bit_adder (
  input  c0,
  input  in_2,
  input  in_3,
  input  in_4,
  input  in_5,
  input  in_6,
  input  in_7,
  input  in_8,
  input  in_9,
  output [3:0] out_10,
  output out_11,
  output out_12
);

  wire and_1_out, and_2_out, and_3_out, and_4_out, and_5_out, and_6_out, and_7_out, and_8_out, and_9_out,
       and_10_out, and_11_out, and_12_out, c1_out, c2_out, c3_out, g3_out, p0_out, p1_out, p2_out, p3_out;

  _1bit_adder_no_carry_out u_1bit_adder_no_carry_out_1 (.A(in_2), .B(in_3), .Sum(out_10[0]), .in_1(c0));
  and and_1 (and_1_out, in_3, in_2);
  or p0 (p0_out, in_3, in_2);
  _1bit_adder_no_carry_out u_1bit_adder_no_carry_out_2 (.A(in_4), .B(in_5), .Sum(out_10[1]), .in_1(c1_out));
  and and_2 (and_2_out, in_5, in_4);
  or p1 (p1_out, in_5, in_4);
  _1bit_adder_no_carry_out u_1bit_adder_no_carry_out_3 (.A(in_6), .B(in_7), .Sum(out_10[2]), .in_1(c2_out));
  and and_3 (and_3_out, in_7, in_6);
  or p2 (p2_out, in_7, in_6);
  _1bit_adder_no_carry_out u_1bit_adder_no_carry_out_4 (.A(in_8), .B(in_9), .Sum(out_10[3]), .in_1(c3_out));
  and g3 (g3_out, in_9, in_8);
  or p3 (p3_out, in_9, in_8);
  and and_4 (and_4_out, c0, p0_out);
  and and_5 (and_5_out, and_1_out, p1_out);
  and and_6 (and_6_out, p1_out, p0_out, c0);
  and and_7 (and_7_out, and_2_out, p2_out);
  and and_8 (and_8_out, p2_out, p1_out, and_1_out);
  and and_9 (and_9_out, p2_out, p1_out, p0_out, c0);
  and P0_2 (out_12, p0_out, p1_out, p2_out, p3_out);
  and and_10 (and_10_out, p3_out, and_3_out);
  and and_11 (and_11_out, p3_out, p2_out, and_2_out);
  and and_12 (and_12_out, p3_out, p2_out, p1_out, and_1_out);
  or c1 (c1_out, and_1_out, and_4_out);
  or c2 (c2_out, and_2_out, and_5_out, and_6_out);
  or c3 (c3_out, and_3_out, and_7_out, and_8_out, and_9_out);
  or G0 (out_11, g3_out, and_10_out, and_11_out, and_12_out);

  // Notes on the sheet:
  //   g0
  //   g1
  //   g2
endmodule

module _1bit_adder_no_carry_out (
  input  in_1,
  input  A,
  input  B,
  output Sum
);

  wire and_1_out, xor_1_out;

  ExactlyOne xor_1 (.out(xor_1_out), .in1(A), .in2(B), .in3(in_1));
  and and_1 (and_1_out, A, B, in_1);
  or or_1 (Sum, xor_1_out, and_1_out);

  // Notes on the sheet:
  //   carry-in
endmodule

module carry_lookahead_unit (
  input  c0,
  input  P0,
  input  G0,
  input  P1,
  input  G1,
  output C1,
  output C2
);

  wire and_1_out, and_2_out, and_3_out;

  and and_1 (and_1_out, c0, P0);
  and and_2 (and_2_out, c0, P0, P1);
  and and_3 (and_3_out, G0, P1);
  or or_1 (C1, and_1_out, G0);
  or or_2 (C2, and_2_out, and_3_out, G1);
endmodule

module _4_bit_signed_adder (
  input  in_1,
  input  in_2,
  input  in_3,
  input  in_4,
  input  in_5,
  input  in_6,
  input  in_7,
  input  in_8,
  input  in_9,
  output [3:0] out_10,
  output OVERFLOW
);

  wire and_1_out, and_2_out, and_3_out, and_4_out, and_5_out, and_6_out, and_7_out, and_8_out, and_9_out,
       and_10_out, and_11_out, c1_out, c2_out, c3_out, p0_out, p1_out, p2_out;

  _1bit_adder_no_carry_out u_1bit_adder_no_carry_out_1 (.A(in_2), .B(in_3), .Sum(out_10[0]), .in_1(in_1));
  and and_1 (and_1_out, in_3, in_2);
  or p0 (p0_out, in_3, in_2);
  _1bit_adder_no_carry_out u_1bit_adder_no_carry_out_2 (.A(in_4), .B(in_5), .Sum(out_10[1]), .in_1(c1_out));
  and and_2 (and_2_out, in_5, in_4);
  or p1 (p1_out, in_5, in_4);
  _1bit_adder_no_carry_out u_1bit_adder_no_carry_out_3 (.A(in_6), .B(in_7), .Sum(out_10[2]), .in_1(c2_out));
  and and_3 (and_3_out, in_7, in_6);
  or p2 (p2_out, in_7, in_6);
  _1bit_adder_no_carry_out u_1bit_adder_no_carry_out_4 (.A(in_8), .B(in_9), .Sum(out_10[3]), .in_1(c3_out));
  and and_4 (and_4_out, ~out_10[3], in_8, in_9);  // AND_Gate
  and and_5 (and_5_out, out_10[3], ~in_8, ~in_9);  // AND_Gate
  and and_6 (and_6_out, in_1, p0_out);
  and and_7 (and_7_out, and_1_out, p1_out);
  and and_8 (and_8_out, p1_out, p0_out, in_1);
  and and_9 (and_9_out, and_2_out, p2_out);
  and and_10 (and_10_out, p2_out, p1_out, and_1_out);
  and and_11 (and_11_out, p2_out, p1_out, p0_out, in_1);
  or or_1 (OVERFLOW, and_4_out, and_5_out);
  or c1 (c1_out, and_1_out, and_6_out);
  or c2 (c2_out, and_2_out, and_7_out, and_8_out);
  or c3 (c3_out, and_3_out, and_9_out, and_10_out, and_11_out);

  // Notes on the sheet:
  //   g0
  //   g1
  //   g2
endmodule
