// Logisim project Group04.circ as structural Verilog: 8 circuits, main circuit 1-Bit Adder (W/O Carry-Out)
module _1_Bit_Adder__W_O_Carry_Out (
  input  Carry_In,
  input  A,
  input  B,
  output Sum
);

  wire and_1_out, and_2_out, and_3_out, and_4_out;

  and and_1 (and_1_out, A, ~B, ~Carry_In);  // AND_Gate
  and and_2 (and_2_out, ~A, B, ~Carry_In);  // AND_Gate
  and and_3 (and_3_out, ~A, ~B, Carry_In);  // AND_Gate
  and and_4 (and_4_out, A, B, Carry_In);
  or or_1 (Sum, and_1_out, and_2_out, and_3_out, and_4_out);
endmodule

module _3_Bit_Decoder (
  input  [2:0] in_1,
  output out_2,
  output out_3,
  output out_4,
  output out_5,
  output out_6,
  output out_7,
  output out_8,
  output out_9
);

  and and_1 (out_2, ~in_1[0], ~in_1[1], ~in_1[2]);  // AND_Gate
  and and_2 (out_3, in_1[0], ~in_1[1], ~in_1[2]);  // AND_Gate
  and and_3 (out_4, ~in_1[0], in_1[1], ~in_1[2]);  // AND_Gate
  and and_4 (out_5, in_1[0], in_1[1], ~in_1[2]);  // AND_Gate
  and and_5 (out_6, ~in_1[0], ~in_1[1], in_1[2]);  // AND_Gate
  and and_6 (out_7, in_1[0], ~in_1[1], in_1[2]);  // AND_Gate
  and and_7 (out_8, ~in_1[0], in_1[1], in_1[2]);  // AND_Gate
  and and_8 (out_9, in_1[0], in_1[1], in_1[2]);
endmodule

module _4_Bit_Adder (
  input  Carry_In,
  input  [3:0] A,
  input  [3:0] B,
  output Super_Carry_Out,
  output [3:0] out_5
);

  wire n4_bit_carry_look_ahead_generator_1_c1, n4_bit_carry_look_ahead_generator_1_c2,
       n4_bit_carry_look_ahead_generator_1_c3;

  _1_Bit_Adder__W_O_Carry_Out u_1_bit_adder_w_o_carry_out_1 (
    .B(A[1]), .A(B[1]), .Sum(out_5[1]), .Carry_In(n4_bit_carry_look_ahead_generator_1_c1));
  _1_Bit_Adder__W_O_Carry_Out u_1_bit_adder_w_o_carry_out_2 (.B(A[0]), .A(B[0]), .Sum(out_5[0]), .Carry_In(Carry_In));
  _1_Bit_Adder__W_O_Carry_Out u_1_bit_adder_w_o_carry_out_3 (
    .B(A[3]), .A(B[3]), .Sum(out_5[3]), .Carry_In(n4_bit_carry_look_ahead_generator_1_c3));
  _1_Bit_Adder__W_O_Carry_Out u_1_bit_adder_w_o_carry_out_4 (
    .B(A[2]), .A(B[2]), .Sum(out_5[2]), .Carry_In(n4_bit_carry_look_ahead_generator_1_c2));
  _4_Bit_Carry_Look_Ahead_Generator u_4_bit_carry_look_ahead_generator_1 (
    .Super_Carry_Out(Super_Carry_Out), .in_1(A), .in_3(B), .CarryOut_1(Carry_In),
    .C1(n4_bit_carry_look_ahead_generator_1_c1), .C2(n4_bit_carry_look_ahead_generator_1_c2),
    .C3(n4_bit_carry_look_ahead_generator_1_c3));  // open: C4
endmodule

module _4_Bit_Carry_Look_Ahead_Generator (
  input  [3:0] in_1,
  input  CarryOut_1,
  input  [3:0] in_3,
  output Super_Carry_Out,
  output C1,
  output C2,
  output C3,
  output C4
);

  wire and_1_out, and_2_out, and_3_out, and_4_out, and_5_out, and_6_out, and_7_out, and_8_out, and_9_out,
       or_1_out, or_2_out, or_3_out, or_4_out, or_5_out;

  and and_1 (and_1_out, in_1[0], in_3[0]);
  or or_1 (or_1_out, in_1[0], in_3[0]);
  C1 c1_1 (.G0(and_1_out), .P0(or_1_out), .C0(CarryOut_1), .c1(C1));
  C2 c2_1 (.G1(and_2_out), .G0(and_1_out), .P0(or_1_out), .P1(or_2_out), .C0(CarryOut_1), .c2(C2));
  or or_2 (or_2_out, in_1[1], in_3[1]);
  and and_2 (and_2_out, in_1[1], in_3[1]);
  C3 c3_1 (
    .G2(and_3_out), .G1(and_2_out), .G0(and_1_out), .P0(or_1_out), .P1(or_2_out), .P2(or_3_out),
    .C0(CarryOut_1), .c3(C3));
  and and_3 (and_3_out, in_1[2], in_3[2]);
  or or_3 (or_3_out, in_1[2], in_3[2]);
  or or_4 (or_4_out, in_1[3], in_3[3]);
  and and_4 (and_4_out, in_1[3], in_3[3]);
  C4 c4_1 (
    .G3(and_4_out), .G2(and_3_out), .G1(and_2_out), .G0(and_1_out), .P0(or_1_out), .P1(or_2_out),
    .P2(or_3_out), .P3(or_4_out), .C0(CarryOut_1), .c4(C4));
  and and_5 (and_5_out, or_3_out, or_4_out, and_2_out);
  and and_6 (and_6_out, or_4_out, and_3_out);
  and and_7 (and_7_out, or_1_out, or_2_out, or_3_out, or_4_out);
  and and_8 (and_8_out, or_2_out, or_3_out, or_4_out, and_1_out);
  or or_5 (or_5_out, and_8_out, and_5_out, and_6_out, and_4_out);
  and and_9 (and_9_out, CarryOut_1, and_7_out);
  or or_6 (Super_Carry_Out, and_9_out, or_5_out);
endmodule

module C1 (
  input  G0,
  input  P0,
  input  C0,
  output c1
);

  wire and_1_out;

  and and_1 (and_1_out, C0, P0);
  or or_1 (c1, and_1_out, G0);
endmodule

module C2 (
  input  G1,
  input  G0,
  input  P0,
  input  P1,
  input  C0,
  output c2
);

  wire and_1_out, and_2_out;

  and and_1 (and_1_out, P0, P1, C0);
  and and_2 (and_2_out, G0, P1);
  or or_1 (c2, G1, and_2_out, and_1_out);
endmodule

module C3 (
  input  G2,
  input  G1,
  input  G0,
  input  P0,
  input  P1,
  input  P2,
  input  C0,
  output c3
);

  wire and_1_out, and_2_out, and_3_out;

  and and_1 (and_1_out, G1, P2);
  and and_2 (and_2_out, P2, P1, G0);
  and and_3 (and_3_out, P0, P1, P2, C0);
  or or_1 (c3, G2, and_1_out, and_2_out, and_3_out);
endmodule

module C4 (
  input  G3,
  input  G2,
  input  G1,
  input  G0,
  input  P0,
  input  P1,
  input  P2,
  input  P3,
  input  C0,
  output c4
);

  wire and_1_out, and_2_out, and_3_out, and_4_out;

  and and_1 (and_1_out, G2, P3);
  and and_2 (and_2_out, G1, P2, P3);
  and and_3 (and_3_out, G0, P1, P2, P3);
  or or_1 (c4, G3, and_1_out, and_2_out, and_3_out, and_4_out);
  and and_4 (and_4_out, P0, P1, P2, P3, C0);
endmodule
