// Logisim project Group05.circ as structural Verilog: 4 circuits, main circuit 1-bit adder for 4-bit
module decoder (
  input  [2:0] in_1,
  output _7,
  output _6,
  output _5,
  output _4,
  output _3,
  output _2,
  output _1,
  output _0
);

  wire not_1_out, not_2_out, not_3_out;

  not not_1 (not_1_out, in_1[0]);
  not not_2 (not_2_out, in_1[1]);
  not not_3 (not_3_out, in_1[2]);
  and and_1 (_7, in_1[0], in_1[1], in_1[2]);
  and and_2 (_5, in_1[0], not_2_out, in_1[2]);
  and and_3 (_6, not_1_out, in_1[1], in_1[2]);
  and and_4 (_4, not_1_out, not_2_out, in_1[2]);
  and and_5 (_3, in_1[0], in_1[1], not_3_out);
  and and_6 (_1, not_3_out, not_2_out, in_1[0]);
  and and_7 (_2, not_1_out, in_1[1], not_3_out);
  and and_8 (_0, not_1_out, not_2_out, not_3_out);

  // Notes on the sheet:
  //   Opdracht 1
endmodule

module _1_bit_adder (
  input  Carry_In,
  input  A,
  input  B,
  output Sum,
  output Carry_Out
);

  wire and_1_out, and_2_out, or_1_out, xor_1_out;

  xor xor_1 (xor_1_out, A, B);
  and and_1 (and_1_out, A, B);
  or or_1 (or_1_out, A, B);
  and and_2 (and_2_out, Carry_In, or_1_out);
  xor xor_2 (Sum, Carry_In, xor_1_out);
  or or_2 (Carry_Out, and_1_out, and_2_out);
endmodule

module _4_bit_adder (
  input  in_1,
  input  [3:0] in_2,
  input  [3:0] in_3,
  output [3:0] out_4,
  output Generate,
  output Propagate
);

  wire and_1_out, and_2_out, and_3_out, and_4_out, and_5_out, and_6_out, and_7_out, and_8_out, and_9_out,
       n1_bit_adder_for_4_bit_1_generate, n1_bit_adder_for_4_bit_1_propagate,
       n1_bit_adder_for_4_bit_2_generate, n1_bit_adder_for_4_bit_2_propagate,
       n1_bit_adder_for_4_bit_3_generate, n1_bit_adder_for_4_bit_3_propagate,
       n1_bit_adder_for_4_bit_4_generate, n1_bit_adder_for_4_bit_4_propagate, or_1_out, or_2_out, or_4_out;

  and and_1 (and_1_out, in_1, n1_bit_adder_for_4_bit_1_propagate);
  _1_bit_adder_for_4_bit u_1_bit_adder_for_4_bit_1 (
    .A(in_2[0]), .B(in_3[0]), .Sum(out_4[0]), .Generate(n1_bit_adder_for_4_bit_1_generate),
    .Propagate(n1_bit_adder_for_4_bit_1_propagate), .Carry_in(in_1));
  or or_1 (or_1_out, and_1_out, n1_bit_adder_for_4_bit_1_generate);
  _1_bit_adder_for_4_bit u_1_bit_adder_for_4_bit_2 (
    .A(in_2[1]), .B(in_3[1]), .Sum(out_4[1]), .Generate(n1_bit_adder_for_4_bit_2_generate),
    .Propagate(n1_bit_adder_for_4_bit_2_propagate), .Carry_in(or_1_out));
  and and_2 (and_2_out, in_1, n1_bit_adder_for_4_bit_2_propagate, n1_bit_adder_for_4_bit_1_propagate);
  or or_2 (or_2_out, and_2_out, and_3_out, n1_bit_adder_for_4_bit_2_generate);
  and and_3 (and_3_out, n1_bit_adder_for_4_bit_2_propagate, n1_bit_adder_for_4_bit_1_generate);
  _1_bit_adder_for_4_bit u_1_bit_adder_for_4_bit_3 (
    .A(in_2[2]), .B(in_3[2]), .Sum(out_4[2]), .Generate(n1_bit_adder_for_4_bit_3_generate),
    .Propagate(n1_bit_adder_for_4_bit_3_propagate), .Carry_in(or_2_out));
  and and_4 (and_4_out, in_1, n1_bit_adder_for_4_bit_1_propagate, n1_bit_adder_for_4_bit_3_propagate, n1_bit_adder_for_4_bit_2_propagate);
  and and_5 (and_5_out, n1_bit_adder_for_4_bit_3_generate, n1_bit_adder_for_4_bit_4_propagate);
  or or_3 (Generate, n1_bit_adder_for_4_bit_4_generate, and_5_out, and_8_out, and_9_out);
  and and_6 (and_6_out, n1_bit_adder_for_4_bit_3_propagate, n1_bit_adder_for_4_bit_2_propagate, n1_bit_adder_for_4_bit_1_generate);
  and and_7 (and_7_out, n1_bit_adder_for_4_bit_3_propagate, n1_bit_adder_for_4_bit_2_generate);
  or or_4 (or_4_out, and_4_out, and_6_out, and_7_out, n1_bit_adder_for_4_bit_3_generate);
  _1_bit_adder_for_4_bit u_1_bit_adder_for_4_bit_4 (
    .A(in_2[3]), .B(in_3[3]), .Sum(out_4[3]), .Generate(n1_bit_adder_for_4_bit_4_generate),
    .Propagate(n1_bit_adder_for_4_bit_4_propagate), .Carry_in(or_4_out));
  and and_8 (and_8_out, n1_bit_adder_for_4_bit_2_generate, n1_bit_adder_for_4_bit_3_propagate, n1_bit_adder_for_4_bit_4_propagate);
  and and_9 (and_9_out, n1_bit_adder_for_4_bit_4_propagate, n1_bit_adder_for_4_bit_2_propagate, n1_bit_adder_for_4_bit_3_propagate, n1_bit_adder_for_4_bit_1_generate);
  and and_10 (Propagate, n1_bit_adder_for_4_bit_4_propagate, n1_bit_adder_for_4_bit_1_propagate, n1_bit_adder_for_4_bit_2_propagate, n1_bit_adder_for_4_bit_3_propagate);

  // Notes on the sheet:
  //   CI0
  //   G0
  //   P0
  //   CI1
  //   P1
  //   G1
  //   CI2
  //   P2
  //   G2
  //   CI3
  //   G3
  //   P3
  //   P3
  //   g1
  //   g2
  //   g0
  //   p2
  //   p1
  //   p0
endmodule

module _1_bit_adder_for_4_bit (
  input  Carry_in,
  input  A,
  input  B,
  output Sum,
  output Generate,
  output Propagate
);

  wire xor_1_out;

  xor xor_1 (xor_1_out, A, B);
  and and_1 (Generate, A, B);
  or or_1 (Propagate, A, B);
  xor xor_2 (Sum, Carry_in, xor_1_out);
endmodule
