// Logisim project Group06.circ as structural Verilog: 4 circuits, main circuit 1-Bit adder
module _1_Bit_adder (
  input  Cin,
  input  a,
  input  b,
  output S,
  output Cout
);

  wire and_1_out, and_2_out, and_3_out, and_4_out, and_5_out, and_6_out, and_7_out, not_1_out, not_2_out,
       not_3_out;

  not not_1 (not_1_out, Cin);
  not not_2 (not_2_out, a);
  not not_3 (not_3_out, b);
  and and_1 (and_1_out, not_1_out, not_3_out, a);
  and and_2 (and_2_out, not_1_out, b, not_2_out);
  and and_3 (and_3_out, Cin, not_2_out, not_3_out);
  and and_4 (and_4_out, Cin, a, b);
  and and_5 (and_5_out, b, Cin);
  and and_6 (and_6_out, a, Cin);
  and and_7 (and_7_out, a, b);
  or or_1 (S, and_1_out, and_2_out, and_3_out, and_4_out);
  or or_2 (Cout, and_5_out, and_6_out, and_7_out);
endmodule

module _4_Bit_adder (
  input  C0,
  input  in_2,
  input  b0_3,
  input  in_4,
  input  in_5,
  input  in_6,
  input  in_7,
  input  in_8,
  input  in_9,
  output PG,
  output GG,
  output Cout,
  output S0,
  output S1,
  output S2,
  output S3
);

  wire n1bit_propgen_adder_1_generate, n1bit_propgen_adder_1_propogate, n1bit_propgen_adder_2_generate,
       n1bit_propgen_adder_2_propogate, n1bit_propgen_adder_3_generate, n1bit_propgen_adder_3_propogate,
       n1bit_propgen_adder_4_generate, n1bit_propgen_adder_4_propogate, n4bit_carry_lookahead_adder_1_c1,
       n4bit_carry_lookahead_adder_1_c2, n4bit_carry_lookahead_adder_1_c3;

  _1bit_PropGen_adder u_1bit_propgen_adder_1 (
    .in_1(C0), .a(in_2), .b(b0_3), .S(S0), .Generate(n1bit_propgen_adder_1_generate),
    .Propogate(n1bit_propgen_adder_1_propogate));
  _1bit_PropGen_adder u_1bit_propgen_adder_2 (
    .in_1(n4bit_carry_lookahead_adder_1_c1), .a(in_4), .b(in_5), .S(S1),
    .Generate(n1bit_propgen_adder_2_generate), .Propogate(n1bit_propgen_adder_2_propogate));
  _1bit_PropGen_adder u_1bit_propgen_adder_3 (
    .in_1(n4bit_carry_lookahead_adder_1_c2), .a(in_6), .b(in_7), .S(S2),
    .Generate(n1bit_propgen_adder_3_generate), .Propogate(n1bit_propgen_adder_3_propogate));
  _1bit_PropGen_adder u_1bit_propgen_adder_4 (
    .in_1(n4bit_carry_lookahead_adder_1_c3), .a(in_8), .b(in_9), .S(S3),
    .Generate(n1bit_propgen_adder_4_generate), .Propogate(n1bit_propgen_adder_4_propogate));
  _4bit_Carry_Lookahead_adder u_4bit_carry_lookahead_adder_1 (
    .p1(n1bit_propgen_adder_1_propogate), .p2(n1bit_propgen_adder_2_propogate),
    .in_3(n1bit_propgen_adder_3_propogate), .Cin(C0), .p3(n1bit_propgen_adder_4_propogate),
    .g0(n1bit_propgen_adder_1_generate), .g1(n1bit_propgen_adder_2_generate),
    .g2(n1bit_propgen_adder_3_generate), .g3(n1bit_propgen_adder_4_generate), .c4(Cout), .G0_2(GG),
    .c1(n4bit_carry_lookahead_adder_1_c1), .c2(n4bit_carry_lookahead_adder_1_c2),
    .c3(n4bit_carry_lookahead_adder_1_c3), .P0(PG));

  // Notes on the sheet:
  //   a0-3
  //   LookAhead
endmodule

module _1bit_PropGen_adder (
  input  in_1,
  input  a,
  input  b,
  output S,
  output Generate,
  output Propogate
);

  wire and_2_out, and_3_out, and_4_out, and_5_out, not_1_out, not_2_out, not_3_out;

  not not_1 (not_1_out, in_1);
  not not_2 (not_2_out, a);
  not not_3 (not_3_out, b);
  and and_1 (Generate, a, b);
  or or_1 (Propogate, a, b);
  and and_2 (and_2_out, not_1_out, not_3_out, a);
  and and_3 (and_3_out, not_1_out, b, not_2_out);
  and and_4 (and_4_out, in_1, not_2_out, not_3_out);
  and and_5 (and_5_out, in_1, a, b);
  or or_2 (S, and_2_out, and_3_out, and_4_out, and_5_out);
endmodule

module _4bit_Carry_Lookahead_adder (
  input  p1,
  input  p2,
  input  in_3,
  input  p3,
  input  g0,
  input  g1,
  input  g2,
  input  g3,
  input  Cin,
  output P0,
  output c4,
  output G0_2,
  output c3,
  output c2,
  output c1
);

  wire and_2_out, and_3_out, and_4_out, and_5_out, and_6_out, and_7_out, and_8_out, and_9_out, and_10_out,
       P0Cin_out;

  and and_1 (P0, p1, p2, in_3, p3);
  and and_2 (and_2_out, p1, Cin);
  or u_c1 (c1, g0, and_2_out);
  and and_3 (and_3_out, p3, in_3, p2, g0);
  and and_4 (and_4_out, p3, in_3, g1);
  and and_5 (and_5_out, p3, g2);
  or or_1 (G0_2, and_3_out, and_4_out, and_5_out, g3);
  and and_6 (and_6_out, g0, p2);
  and and_7 (and_7_out, Cin, p1, p2);
  or u_c2 (c2, g1, and_6_out, and_7_out);
  and P0Cin (P0Cin_out, P0, Cin);
  or or_2 (c4, G0_2, P0Cin_out);
  and and_8 (and_8_out, in_3, g1);
  and and_9 (and_9_out, in_3, p2, g0);
  and and_10 (and_10_out, in_3, p2, p1, Cin);
  or u_c3 (c3, g2, and_8_out, and_9_out, and_10_out);

  // Notes on the sheet:
  //   p0
  //   g0-2
  //   p0-3
  //   g0
  //   p0c0
  //   p3p2p1g0
  //   p3p2g1
  //   p3g2
  //   g3
  //   g1
  //   p1g0
  //   p1p0c0
  //   g2
  //   p2g1
  //   p2p1g0
  //   p2p1p0c0
endmodule
