// Logisim project Group07.circ as structural Verilog: 4 circuits, main circuit 1-bit adder zonder XOR
module _1_bit_adder_zonder_XOR (
  input  Cin,
  input  A,
  input  B,
  output SOM,
  output out_5
);

  wire and_1_out, and_2_out, and_3_out, and_4_out, and_5_out, and_6_out, and_7_out, not_1_out, not_2_out,
       not_3_out;

  not not_1 (not_1_out, B);
  not not_2 (not_2_out, A);
  not not_3 (not_3_out, Cin);
  and and_1 (and_1_out, Cin, B);
  and and_2 (and_2_out, A, Cin);
  and and_3 (and_3_out, A, B);
  and and_4 (and_4_out, Cin, not_2_out, not_1_out);
  and and_5 (and_5_out, B, not_3_out, not_2_out);
  and and_6 (and_6_out, A, not_1_out, not_3_out);
  and and_7 (and_7_out, Cin, A, B);
  or or_1 (SOM, and_4_out, and_5_out, and_6_out, and_7_out);
  or or_2 (out_5, and_1_out, and_2_out, and_3_out);
endmodule

module _1_Bit_Adder (
  input  A,
  input  B,
  input  Cin,
  output Som,
  output Cout
);

  wire and_1_out, and_2_out, xor_1_out;

  xor xor_1 (xor_1_out, A, B);
  xor xor_2 (Som, xor_1_out, Cin);
  and and_1 (and_1_out, xor_1_out, Cin);
  and and_2 (and_2_out, A, B);
  or or_1 (Cout, and_1_out, and_2_out);
endmodule

module _1_Bit_look_ahead (
  input  A,
  input  B,
  input  Cin,
  output g,
  output p,
  output sum
);

  wire xor_1_out;

  xor xor_1 (xor_1_out, A, B);
  and and_1 (g, A, B);
  or or_1 (p, A, B);
  xor xor_2 (sum, xor_1_out, Cin);
endmodule

module _4_bit_Carry_Look_Ahead (
  input  [3:0] A,
  input  C0,
  input  [3:0] B,
  output [3:0] som,
  output g,
  output p
);

  wire and_1_out, and_2_out, and_3_out, and_4_out, and_5_out, and_6_out, and_8_out, and_9_out, and_10_out,
       n1_bit_look_ahead_1_g, n1_bit_look_ahead_1_p, n1_bit_look_ahead_2_g, n1_bit_look_ahead_2_p,
       n1_bit_look_ahead_3_g, n1_bit_look_ahead_3_p, n1_bit_look_ahead_4_g, n1_bit_look_ahead_4_p, or_1_out,
       or_2_out, or_3_out;

  _1_Bit_look_ahead u_1_bit_look_ahead_1 (
    .A(A[0]), .B(B[0]), .Cin(C0), .g(n1_bit_look_ahead_1_g), .p(n1_bit_look_ahead_1_p), .sum(som[0]));
  _1_Bit_look_ahead u_1_bit_look_ahead_2 (
    .A(A[1]), .B(B[1]), .Cin(or_1_out), .g(n1_bit_look_ahead_2_g), .p(n1_bit_look_ahead_2_p), .sum(som[1]));
  _1_Bit_look_ahead u_1_bit_look_ahead_3 (
    .A(A[2]), .B(B[2]), .Cin(or_2_out), .g(n1_bit_look_ahead_3_g), .p(n1_bit_look_ahead_3_p), .sum(som[2]));
  _1_Bit_look_ahead u_1_bit_look_ahead_4 (
    .A(A[3]), .B(B[3]), .Cin(or_3_out), .g(n1_bit_look_ahead_4_g), .p(n1_bit_look_ahead_4_p), .sum(som[3]));
  and and_1 (and_1_out, C0, n1_bit_look_ahead_1_p);
  or or_1 (or_1_out, and_1_out, n1_bit_look_ahead_1_g);
  and and_2 (and_2_out, n1_bit_look_ahead_1_g, n1_bit_look_ahead_2_p);
  and and_3 (and_3_out, n1_bit_look_ahead_2_p, n1_bit_look_ahead_1_p, C0);
  and and_4 (and_4_out, n1_bit_look_ahead_3_p, n1_bit_look_ahead_2_p, n1_bit_look_ahead_1_p, C0);
  and and_5 (and_5_out, n1_bit_look_ahead_3_p, n1_bit_look_ahead_2_p, n1_bit_look_ahead_1_g);
  and and_6 (and_6_out, n1_bit_look_ahead_3_p, n1_bit_look_ahead_2_g);
  or or_2 (or_2_out, and_2_out, and_3_out, n1_bit_look_ahead_2_g);
  or or_3 (or_3_out, and_4_out, and_5_out, and_6_out, n1_bit_look_ahead_3_g);
  and and_7 (p, n1_bit_look_ahead_4_p, n1_bit_look_ahead_3_p, n1_bit_look_ahead_2_p, n1_bit_look_ahead_1_p);
  and and_8 (and_8_out, n1_bit_look_ahead_4_p, n1_bit_look_ahead_3_g);
  and and_9 (and_9_out, n1_bit_look_ahead_4_p, n1_bit_look_ahead_3_p, n1_bit_look_ahead_2_g);
  and and_10 (and_10_out, n1_bit_look_ahead_4_p, n1_bit_look_ahead_3_p, n1_bit_look_ahead_2_p, n1_bit_look_ahead_1_g);
  or or_4 (g, n1_bit_look_ahead_4_g, and_8_out, and_9_out, and_10_out);
endmodule
