// Logisim project Group08.circ as structural Verilog: 4 circuits, main circuit 1bit adder
// 1bit +
module _1bit_adder (
  input  CarryIn,
  input  A,
  input  B,
  output Sum,
  output CarryOut
);

  wire and_1_out, and_2_out, and_3_out, and_4_out, and_5_out, and_6_out, and_7_out;

  and and_1 (and_1_out, ~A, ~B, CarryIn);  // AND_Gate
  and and_2 (and_2_out, ~A, B, ~CarryIn);  // AND_Gate
  and and_3 (and_3_out, A, ~B, ~CarryIn);  // AND_Gate
  and and_4 (and_4_out, A, B, CarryIn);
  and and_5 (and_5_out, A, B);
  and and_6 (and_6_out, A, CarryIn);
  and and_7 (and_7_out, B, CarryIn);
  or or_1 (Sum, and_1_out, and_2_out, and_3_out, and_4_out);
  or or_2 (CarryOut, and_5_out, and_6_out, and_7_out);
endmodule

module _1bit_zonder_cout (
  input  CarryIn,
  input  A,
  input  B,
  output Sum
);

  wire and_1_out, and_2_out, and_3_out, and_4_out;

  and and_1 (and_1_out, ~A, ~B, CarryIn);  // AND_Gate
  and and_2 (and_2_out, ~A, B, ~CarryIn);  // AND_Gate
  and and_3 (and_3_out, A, ~B, ~CarryIn);  // AND_Gate
  and and_4 (and_4_out, A, B, CarryIn);
  or or_1 (Sum, and_1_out, and_2_out, and_3_out, and_4_out);
endmodule

module _4_bit_lookahead (
  input  in_1,
  input  [3:0] in_2,
  input  [3:0] in_3,
  output [3:0] out_4,
  output P,
  output G
);

  wire and_1_out, and_2_out, and_3_out, and_4_out, and_5_out, and_6_out, and_7_out, and_8_out, and_9_out,
       and_10_out, and_11_out, and_12_out, and_13_out, or_1_out, or_2_out, or_3_out, or_4_out, or_5_out,
       or_6_out, p0_out;

  or or_1 (or_1_out, in_3[2], in_2[2]);
  and and_1 (and_1_out, in_3[2], in_2[2]);
  or or_2 (or_2_out, in_2[3], in_3[3]);
  and and_2 (and_2_out, in_2[3], in_3[3]);
  or p0 (p0_out, in_2[0], in_3[0]);
  and and_3 (and_3_out, in_2[0], in_3[0]);
  or or_3 (or_3_out, in_2[1], in_3[1]);
  and and_4 (and_4_out, in_2[1], in_3[1]);
  and and_5 (and_5_out, and_4_out, or_1_out);
  and and_6 (and_6_out, in_1, p0_out);
  and and_7 (and_7_out, and_3_out, or_3_out);
  and and_8 (and_8_out, in_1, p0_out, or_3_out);
  and and_9 (and_9_out, and_3_out, or_3_out, or_1_out);
  or or_4 (or_4_out, and_6_out, and_3_out);
  or or_5 (or_5_out, and_7_out, and_8_out, and_4_out);
  and and_10 (and_10_out, in_1, p0_out, or_3_out, or_1_out);
  or or_6 (or_6_out, and_10_out, and_9_out, and_5_out, and_1_out);
  and and_11 (and_11_out, or_2_out, or_1_out, and_4_out);
  and and_12 (and_12_out, and_3_out, or_3_out, or_1_out, or_2_out);
  _1bit_zonder_cout u_1bit_zonder_cout_1 (.A(in_2[0]), .B(in_3[0]), .CarryIn(in_1), .Sum(out_4[0]));
  _1bit_zonder_cout u_1bit_zonder_cout_2 (.A(in_2[1]), .B(in_3[1]), .CarryIn(or_4_out), .Sum(out_4[1]));
  _1bit_zonder_cout u_1bit_zonder_cout_3 (.A(in_2[2]), .B(in_3[2]), .CarryIn(or_5_out), .Sum(out_4[2]));
  _1bit_zonder_cout u_1bit_zonder_cout_4 (.A(in_2[3]), .B(in_3[3]), .CarryIn(or_6_out), .Sum(out_4[3]));
  and and_13 (and_13_out, or_2_out, and_1_out);
  and and_14 (P, p0_out, or_3_out, or_1_out, or_2_out);
  or or_7 (G, and_2_out, and_13_out, and_11_out, and_12_out);
endmodule

module _4_bit_lookahead_simplified (
  input  in_1,
  input  [3:0] in_2,
  input  [3:0] in_3,
  output [3:0] out_4,
  output P,
  output G
);

  wire and_1_out, and_2_out, and_3_out, and_4_out, and_5_out, and_6_out, and_7_out, and_8_out, and_9_out,
       and_10_out, and_11_out, and_12_out, and_13_out, and_14_out, and_15_out, and_16_out, and_17_out,
       and_18_out, and_19_out, and_20_out, and_21_out, and_22_out, and_23_out, and_24_out, and_25_out,
       and_27_out, and_28_out, and_29_out, and_30_out, and_31_out, and_32_out, and_33_out, C1_out, C2_out,
       C3_out, or_1_out, or_2_out, or_3_out, or_4_out;

  and and_1 (and_1_out, in_2[0], in_3[0]);
  and and_2 (and_2_out, in_1, in_2[0]);
  or C1 (C1_out, and_1_out, and_2_out, and_3_out);
  and and_3 (and_3_out, in_1, in_3[0]);
  and and_4 (and_4_out, in_2[1], in_3[1]);
  and and_5 (and_5_out, in_2[0], in_3[0], in_3[1]);
  and and_6 (and_6_out, in_2[0], in_2[1], in_3[0]);
  and and_7 (and_7_out, in_1, in_2[1], in_3[0]);
  and and_8 (and_8_out, in_1, in_2[0], in_2[1]);
  and and_9 (and_9_out, in_1, in_2[0], in_3[1]);
  and and_10 (and_10_out, in_1, in_3[0], in_3[1]);
  or C2 (C2_out, and_4_out, and_6_out, and_5_out, and_8_out, and_7_out, and_9_out, and_10_out);
  and and_11 (and_11_out, in_2[2], in_3[2]);
  and and_12 (and_12_out, in_2[1], in_2[2], in_3[1]);
  and and_13 (and_13_out, in_2[1], in_3[1], in_3[2]);
  and and_14 (and_14_out, in_2[0], in_2[1], in_2[2], in_3[0]);
  and and_15 (and_15_out, in_2[0], in_2[2], in_3[0], in_3[1]);
  and and_16 (and_16_out, in_1, in_2[0], in_2[1], in_2[2]);
  and and_17 (and_17_out, in_1, in_2[1], in_2[2], in_3[0]);
  and and_18 (and_18_out, in_1, in_2[1], in_2[2], in_3[1]);
  and and_19 (and_19_out, in_1, in_2[2], in_3[0], in_3[1]);
  and and_20 (and_20_out, in_2[0], in_2[1], in_3[0], in_3[2]);
  and and_21 (and_21_out, in_2[0], in_3[0], in_3[1], in_3[2]);
  and and_22 (and_22_out, in_1, in_2[0], in_2[1], in_3[2]);
  and and_23 (and_23_out, in_1, in_2[1], in_3[0], in_3[2]);
  and and_24 (and_24_out, in_1, in_2[0], in_3[1], in_3[2]);
  and and_25 (and_25_out, in_1, in_3[0], in_3[1], in_3[2]);
  or or_1 (or_1_out, in_2[0], in_3[0]);
  or or_2 (or_2_out, in_2[1], in_3[1]);
  or or_3 (or_3_out, in_2[2], in_3[2]);
  and and_26 (P, or_1_out, or_2_out, or_3_out, or_4_out);
  or C3 (C3_out, and_11_out, and_12_out, and_13_out, and_14_out, and_15_out, and_16_out, and_17_out, and_18_out, and_19_out, and_20_out, and_21_out, and_22_out, and_23_out, and_24_out, and_25_out);
  or or_4 (or_4_out, in_2[3], in_3[3]);
  and and_27 (and_27_out, in_2[0], in_3[0]);
  and and_28 (and_28_out, or_2_out, or_3_out, and_27_out, or_4_out);
  and and_29 (and_29_out, in_2[2], in_3[2]);
  and and_30 (and_30_out, in_2[1], in_3[1]);
  and and_31 (and_31_out, and_30_out, or_3_out, or_4_out);
  and and_32 (and_32_out, and_29_out, or_4_out);
  or or_5 (G, and_28_out, and_31_out, and_32_out, and_33_out);
  and and_33 (and_33_out, in_2[3], in_3[3]);
  _1bit_zonder_cout u_1bit_zonder_cout_1 (.A(in_2[0]), .B(in_3[0]), .CarryIn(in_1), .Sum(out_4[0]));
  _1bit_zonder_cout u_1bit_zonder_cout_2 (.A(in_2[1]), .B(in_3[1]), .CarryIn(C1_out), .Sum(out_4[1]));
  _1bit_zonder_cout u_1bit_zonder_cout_3 (.A(in_2[2]), .B(in_3[2]), .CarryIn(C2_out), .Sum(out_4[2]));
  _1bit_zonder_cout u_1bit_zonder_cout_4 (.A(in_2[3]), .B(in_3[3]), .CarryIn(C3_out), .Sum(out_4[3]));
endmodule
