// Logisim project Group09.circ as structural Verilog: 3 circuits, main circuit 1-Bit Full Adder
module _1_Bit_Full_Adder (
  input  Carry_in,
  input  A,
  input  B,
  output Sum,
  output Carry_out
);

  wire and_1_out, and_2_out, and_3_out, and_4_out, and_5_out, and_6_out, and_7_out, not_1_out, not_2_out,
       not_3_out;

  not not_1 (not_1_out, Carry_in);
  not not_2 (not_2_out, A);
  not not_3 (not_3_out, B);
  and and_1 (and_1_out, A, not_3_out, not_1_out);
  and and_2 (and_2_out, not_2_out, not_3_out, Carry_in);
  and and_3 (and_3_out, not_2_out, B, not_1_out);
  and and_4 (and_4_out, B, A, Carry_in);
  or or_1 (Sum, and_4_out, and_2_out, and_3_out, and_1_out);
  and and_5 (and_5_out, A, Carry_in);
  and and_6 (and_6_out, B, Carry_in);
  and and_7 (and_7_out, B, A);
  or or_2 (Carry_out, and_7_out, and_5_out, and_6_out);
endmodule

// Adder
module _1_Bit_simple_adder (
  input  Carry_in,
  input  A,
  input  B,
  output Sum
);

  wire and_1_out, and_2_out, and_3_out, and_4_out, not_1_out, not_2_out, not_3_out;

  not not_1 (not_1_out, Carry_in);
  not not_2 (not_2_out, A);
  not not_3 (not_3_out, B);
  and and_1 (and_1_out, A, not_3_out, not_1_out);
  and and_2 (and_2_out, not_2_out, not_3_out, Carry_in);
  and and_3 (and_3_out, not_2_out, B, not_1_out);
  and and_4 (and_4_out, B, A, Carry_in);
  or or_1 (Sum, and_4_out, and_2_out, and_3_out, and_1_out);
endmodule

module _4_bit_cla (
  input  C_in,
  input  [3:0] A,
  input  [3:0] B,
  output G,
  output P,
  output [3:0] SUM
);

  wire c1_out, c2_out, c3_out, g0_out, g0p1p2p3_out, g1_out, g1p2p3_out, g2_out, g2p3_out, g3_out, p0_out,
       p0c0_out, p1_out, p1g0_out, p1p0c0_out, p2_out, p2g1_out, p2p1g0_out, p2p1p0c0_out, p3_out;

  and g0 (g0_out, A[0], B[0]);
  or p0 (p0_out, A[0], B[0]);
  and g1 (g1_out, A[1], B[1]);
  or p1 (p1_out, A[1], B[1]);
  and g2 (g2_out, A[2], B[2]);
  or p2 (p2_out, A[2], B[2]);
  and g3 (g3_out, A[3], B[3]);
  or p3 (p3_out, A[3], B[3]);
  and g2p3 (g2p3_out, g2_out, p3_out);
  and g1p2p3 (g1p2p3_out, g1_out, p3_out, p2_out);
  and g0p1p2p3 (g0p1p2p3_out, g0_out, p3_out, p2_out, p1_out);
  and p3p2p1p0 (P, p0_out, p1_out, p2_out, p3_out);
  and p2p1p0c0 (p2p1p0c0_out, p2_out, p1_out, p0_out, C_in);
  and p2p1g0 (p2p1g0_out, p2_out, p1_out, g0_out);
  and p2g1 (p2g1_out, p2_out, g1_out);
  and p1g0 (p1g0_out, p1_out, g0_out);
  and p1p0c0 (p1p0c0_out, p1_out, p0_out, C_in);
  and p0c0 (p0c0_out, p0_out, C_in);
  or c3 (c3_out, p2p1p0c0_out, p2p1g0_out, p2g1_out, g2_out);
  or c2 (c2_out, p1g0_out, g1_out, p1p0c0_out);
  or c1 (c1_out, g0_out, p0c0_out);
  _1_Bit_simple_adder u_1_bit_simple_adder_1 (.Carry_in(c1_out), .A(B[1]), .B(A[1]), .Sum(SUM[1]));
  _1_Bit_simple_adder u_1_bit_simple_adder_2 (.Carry_in(C_in), .A(B[0]), .B(A[0]), .Sum(SUM[0]));
  or or_1 (G, g2p3_out, g1p2p3_out, g0p1p2p3_out, g3_out);
  _1_Bit_simple_adder u_1_bit_simple_adder_3 (.Carry_in(c2_out), .A(B[2]), .B(A[2]), .Sum(SUM[2]));
  _1_Bit_simple_adder u_1_bit_simple_adder_4 (.Carry_in(c3_out), .A(B[3]), .B(A[3]), .Sum(SUM[3]));
endmodule
