// Logisim project Group10.circ as structural Verilog: 5 circuits, main circuit proj2.oef1
module proj2_oef3 (
  input  Carryin,
  input  Input_A,
  input  Input_B,
  output out_4,
  output out_5
);

  wire and_1_out, and_2_out, and_3_out, and_4_out, and_5_out, and_6_out, and_7_out, not_1_out, not_2_out,
       not_3_out, not_4_out, not_5_out, not_6_out;

  and and_1 (and_1_out, Input_B, Input_A);
  and and_2 (and_2_out, Input_B, Carryin);
  or or_1 (out_5, and_1_out, and_2_out, and_3_out);
  and and_3 (and_3_out, Input_A, Carryin);
  not not_1 (not_1_out, Carryin);
  and and_4 (and_4_out, not_1_out, not_2_out, Input_B);
  not not_2 (not_2_out, Input_A);
  not not_3 (not_3_out, Carryin);
  and and_5 (and_5_out, not_3_out, Input_A, not_4_out);
  not not_4 (not_4_out, Input_B);
  and and_6 (and_6_out, Carryin, not_5_out, not_6_out);
  not not_5 (not_5_out, Input_A);
  not not_6 (not_6_out, Input_B);
  and and_7 (and_7_out, Carryin, Input_A, Input_B);
  or or_2 (out_4, and_4_out, and_5_out, and_6_out, and_7_out);

  // Notes on the sheet:
  //   Carryout
  //   sum
endmodule

module proj2_oef1 (
  input  [2:0] in_1,
  output out_2,
  output out_3,
  output out_4,
  output out_5,
  output out_6,
  output out_7,
  output out_8,
  output out_9
);

  wire not_1_out, not_2_out, not_3_out;

  not not_1 (not_1_out, in_1[2]);
  not not_2 (not_2_out, in_1[1]);
  not not_3 (not_3_out, in_1[0]);
  and and_1 (out_2, not_1_out, not_2_out, not_3_out);
  and and_2 (out_3, not_1_out, not_2_out, in_1[0]);
  and and_3 (out_4, not_1_out, in_1[1], not_3_out);
  and and_4 (out_5, not_1_out, in_1[1], in_1[0]);
  and and_5 (out_6, in_1[2], not_2_out, not_3_out);
  and and_6 (out_7, in_1[2], not_2_out, in_1[0]);
  and and_7 (out_8, in_1[2], in_1[1], not_3_out);
  and and_8 (out_9, in_1[2], in_1[1], in_1[0]);
endmodule

module proj2_oef5___4_bit_adder_block (
  input  in_1,
  input  [3:0] A,
  input  [3:0] B,
  output [3:0] out_4,
  output out_5,
  output out_6,
  output out_7
);

  wire and_1_out, and_2_out, and_3_out, and_4_out, and_5_out, and_6_out, and_7_out, and_8_out, and_10_out,
       and_11_out, and_12_out, or_1_out, or_2_out, or_3_out, or_4_out, or_5_out, or_6_out, or_8_out;

  and and_1 (and_1_out, in_1, or_2_out);
  or or_1 (or_1_out, and_1_out, and_2_out);
  or or_2 (or_2_out, A[0], B[0]);
  and and_2 (and_2_out, A[0], B[0]);
  adder_no_carryout adder_no_carryout_1 (.in_2(A[0]), .in_3(B[0]), .in_1(in_1), .out_4(out_4[0]));
  or or_3 (or_3_out, and_3_out, and_4_out);
  and and_3 (and_3_out, or_1_out, or_4_out);
  or or_4 (or_4_out, A[1], B[1]);
  adder_no_carryout adder_no_carryout_2 (.in_2(A[1]), .in_3(B[1]), .in_1(or_1_out), .out_4(out_4[1]));
  and and_4 (and_4_out, A[1], B[1]);
  adder_no_carryout adder_no_carryout_3 (.in_2(A[2]), .in_3(B[2]), .in_1(or_3_out), .out_4(out_4[2]));
  or or_5 (or_5_out, and_5_out, and_6_out);
  and and_5 (and_5_out, or_3_out, or_6_out);
  or or_6 (or_6_out, A[2], B[2]);
  and and_6 (and_6_out, A[2], B[2]);
  adder_no_carryout adder_no_carryout_4 (.in_2(A[3]), .in_3(B[3]), .in_1(or_5_out), .out_4(out_4[3]));
  or or_7 (out_5, and_7_out, and_8_out);
  and and_7 (and_7_out, or_5_out, or_8_out);
  or or_8 (or_8_out, A[3], B[3]);
  and and_8 (and_8_out, A[3], B[3]);
  and and_9 (out_6, or_2_out, or_4_out, or_6_out, or_8_out);
  and and_10 (and_10_out, or_4_out, or_6_out, or_8_out, and_2_out);
  and and_11 (and_11_out, or_6_out, or_8_out, and_4_out);
  and and_12 (and_12_out, or_8_out, and_6_out);
  or or_9 (out_7, and_10_out, and_11_out, and_12_out, and_8_out);

  // Notes on the sheet:
  //   Ci0
  //   Ci1
  //   Cin-1 * pn-1
  //   p0
  //   g0
  //   Cin-1 * pn-1
  //   p1
  //   Ci2
  //   g1
  //   Ci3
  //   Cin-1 * pn-1
  //   p2
  //   g2
  //   Cin-1 * pn-1
  //   Ci4
  //   p3
  //   g3
  //   -> Generate een signaal en propagate het, maar geeft ook binnenkomend signaal door!
  //   Ci4 (carryin van volgend 4-bit adder block)
  //   Superpropagate en SuperGenerate kan op hetzelfde moment! 
  //   P0 (superpropagate)
  //   G0(Supergenerate)
endmodule

module adder_no_carryout (
  input  in_1,
  input  in_2,
  input  in_3,
  output out_4
);

  wire and_1_out, and_2_out, and_3_out, and_4_out, not_1_out, not_2_out, not_3_out, not_4_out, not_5_out,
       not_6_out;

  not not_1 (not_1_out, in_1);
  and and_1 (and_1_out, not_1_out, not_2_out, in_3);
  not not_2 (not_2_out, in_2);
  not not_3 (not_3_out, in_1);
  and and_2 (and_2_out, not_3_out, in_2, not_4_out);
  not not_4 (not_4_out, in_3);
  and and_3 (and_3_out, in_1, not_5_out, not_6_out);
  not not_5 (not_5_out, in_2);
  not not_6 (not_6_out, in_3);
  and and_4 (and_4_out, in_1, in_2, in_3);
  or or_1 (out_4, and_1_out, and_2_out, and_3_out, and_4_out);
endmodule

module proj2_oef5_b___optimised_4_bit_adder (
  input  in_1,
  input  [3:0] A,
  input  [3:0] B,
  output [3:0] out_4,
  output out_5,
  output out_6,
  output out_7
);

  wire and_1_out, and_2_out, and_3_out, and_4_out, and_5_out, and_6_out, and_7_out, and_8_out, and_10_out,
       and_11_out, and_12_out, or_1_out, or_2_out, or_3_out, or_4_out, or_5_out, or_6_out, or_8_out;

  and and_1 (and_1_out, in_1, or_2_out);
  or or_1 (or_1_out, and_1_out, and_2_out);
  or or_2 (or_2_out, A[0], B[0]);
  and and_2 (and_2_out, A[0], B[0]);
  adder_no_carryout adder_no_carryout_1 (.in_2(A[0]), .in_3(B[0]), .in_1(in_1), .out_4(out_4[0]));
  or or_3 (or_3_out, and_3_out, and_4_out);
  and and_3 (and_3_out, or_1_out, or_4_out);
  or or_4 (or_4_out, A[1], B[1]);
  adder_no_carryout adder_no_carryout_2 (.in_2(A[1]), .in_3(B[1]), .in_1(or_1_out), .out_4(out_4[1]));
  and and_4 (and_4_out, A[1], B[1]);
  adder_no_carryout adder_no_carryout_3 (.in_2(A[2]), .in_3(B[2]), .in_1(or_3_out), .out_4(out_4[2]));
  or or_5 (or_5_out, and_5_out, and_6_out);
  and and_5 (and_5_out, or_3_out, or_6_out);
  or or_6 (or_6_out, A[2], B[2]);
  and and_6 (and_6_out, A[2], B[2]);
  adder_no_carryout adder_no_carryout_4 (.in_2(A[3]), .in_3(B[3]), .in_1(or_5_out), .out_4(out_4[3]));
  or or_7 (out_5, and_7_out, and_8_out);
  and and_7 (and_7_out, or_5_out, or_8_out);
  or or_8 (or_8_out, A[3], B[3]);
  and and_8 (and_8_out, A[3], B[3]);
  and and_9 (out_6, or_2_out, or_4_out, or_6_out, or_8_out);
  and and_10 (and_10_out, or_4_out, or_6_out, or_8_out, and_2_out);
  and and_11 (and_11_out, or_6_out, or_8_out, and_4_out);
  and and_12 (and_12_out, or_8_out, and_6_out);
  or or_9 (out_7, and_10_out, and_11_out, and_12_out, and_8_out);

  // Notes on the sheet:
  //   Ci0
  //   Ci1
  //   Cin-1 * pn-1
  //   p0
  //   g0
  //   Cin-1 * pn-1
  //   p1
  //   Ci2
  //   g1
  //   Ci3
  //   Cin-1 * pn-1
  //   p2
  //   g2
  //   Cin-1 * pn-1
  //   Ci4
  //   p3
  //   g3
  //   -> Generate een signaal en propagate het, maar geeft ook binnenkomend signaal door!
  //   Ci4 (carryin van volgend 4-bit adder block)
  //   Superpropagate en SuperGenerate kan op hetzelfde moment! 
  //   P0 (superpropagate)
  //   G0(Supergenerate)
endmodule
