// Logisim project Group11.circ as structural Verilog: 5 circuits, main circuit 1BIT adder
module _1BIT_adder (
  input  CarryIn,
  input  A,
  input  B,
  output Sum,
  output CarryOut
);

  wire and_1_out, and_2_out, and_3_out, and_4_out, and_5_out, and_6_out, and_7_out;

  and and_1 (and_1_out, ~CarryIn, A, ~B);  // AND_Gate
  and and_2 (and_2_out, ~CarryIn, ~A, B);  // AND_Gate
  and and_3 (and_3_out, CarryIn, ~A, ~B);  // AND_Gate
  and and_4 (and_4_out, CarryIn, A, B);
  and and_5 (and_5_out, CarryIn, B);
  or or_1 (CarryOut, and_5_out, and_6_out, and_7_out);
  and and_6 (and_6_out, CarryIn, A);
  and and_7 (and_7_out, A, B);
  or or_2 (Sum, and_1_out, and_2_out, and_3_out, and_4_out);
endmodule

module _1BIT_lookahead_adder (
  input  CarryIn,
  input  A,
  input  B,
  output Sum,
  output Generate,
  output Propagate
);

  wire and_1_out, and_2_out, and_3_out, and_4_out;

  and and_1 (and_1_out, ~CarryIn, A, ~B);  // AND_Gate
  and and_2 (and_2_out, ~CarryIn, ~A, B);  // AND_Gate
  and and_3 (and_3_out, CarryIn, ~A, ~B);  // AND_Gate
  and and_4 (and_4_out, CarryIn, A, B);
  and and_5 (Generate, A, B);
  or or_1 (Propagate, A, B);
  or or_2 (Sum, and_1_out, and_2_out, and_3_out, and_4_out);
endmodule

module _4BIT_lookahead_adder (
  input  CarryIn,
  input  [3:0] A,
  input  [3:0] B,
  output Super_Propagate,
  output Super_Generate,
  output [3:0] Sum
);

  wire n1bit_lookahead_adder_1_generate, n1bit_lookahead_adder_1_propagate, n1bit_lookahead_adder_2_generate,
       n1bit_lookahead_adder_2_propagate, n1bit_lookahead_adder_3_generate,
       n1bit_lookahead_adder_3_propagate, n1bit_lookahead_adder_4_generate,
       n1bit_lookahead_adder_4_propagate, n4bit_lookahead_unit_1_c1, n4bit_lookahead_unit_1_c2,
       n4bit_lookahead_unit_1_c3;

  _1BIT_lookahead_adder u_1bit_lookahead_adder_1 (
    .A(A[0]), .B(B[0]), .Sum(Sum[0]), .Generate(n1bit_lookahead_adder_1_generate),
    .Propagate(n1bit_lookahead_adder_1_propagate), .CarryIn(CarryIn));
  _1BIT_lookahead_adder u_1bit_lookahead_adder_2 (
    .A(A[1]), .B(B[1]), .Sum(Sum[1]), .Generate(n1bit_lookahead_adder_2_generate),
    .Propagate(n1bit_lookahead_adder_2_propagate), .CarryIn(n4bit_lookahead_unit_1_c1));
  _1BIT_lookahead_adder u_1bit_lookahead_adder_3 (
    .A(A[2]), .B(B[2]), .Sum(Sum[2]), .Generate(n1bit_lookahead_adder_3_generate),
    .Propagate(n1bit_lookahead_adder_3_propagate), .CarryIn(n4bit_lookahead_unit_1_c2));
  _1BIT_lookahead_adder u_1bit_lookahead_adder_4 (
    .A(A[3]), .B(B[3]), .Sum(Sum[3]), .Generate(n1bit_lookahead_adder_4_generate),
    .Propagate(n1bit_lookahead_adder_4_propagate), .CarryIn(n4bit_lookahead_unit_1_c3));
  _4bit_lookahead_unit u_4bit_lookahead_unit_1 (
    .G0(n1bit_lookahead_adder_1_generate), .P0(n1bit_lookahead_adder_1_propagate),
    .G1(n1bit_lookahead_adder_2_generate), .P1(n1bit_lookahead_adder_2_propagate),
    .G2(n1bit_lookahead_adder_3_generate), .P2(n1bit_lookahead_adder_3_propagate),
    .G3(n1bit_lookahead_adder_4_generate), .P3(n1bit_lookahead_adder_4_propagate),
    .C1(n4bit_lookahead_unit_1_c1), .C2(n4bit_lookahead_unit_1_c2), .C3(n4bit_lookahead_unit_1_c3),
    .Super_Propagate(Super_Propagate), .Super_Generate(Super_Generate), .CarryIn(CarryIn));  // open: out_13
endmodule

module _4bit_lookahead_unit (
  input  CarryIn,
  input  G0,
  input  P0,
  input  G1,
  input  P1,
  input  G2,
  input  P2,
  input  G3,
  input  P3,
  output C1,
  output C2,
  output C3,
  output out_13,
  output Super_Propagate,
  output Super_Generate
);

  wire and_1_out, and_2_out, and_3_out, and_4_out, and_5_out, and_6_out, and_7_out, and_8_out, and_9_out,
       and_10_out, and_12_out, and_13_out, and_14_out;

  and and_1 (and_1_out, CarryIn, P0);
  and and_2 (and_2_out, G0, P1);
  and and_3 (and_3_out, P1, P0, CarryIn);
  and and_4 (and_4_out, P2, G1);
  and and_5 (and_5_out, P2, P1, G0);
  and and_6 (and_6_out, P2, P1, P0, CarryIn);
  and and_7 (and_7_out, P3, G2);
  and and_8 (and_8_out, P3, P2, G1);
  and and_9 (and_9_out, P3, P2, P1, G0);
  and and_10 (and_10_out, P3, P2, P1, P0, CarryIn);
  and and_11 (Super_Propagate, P0, P1, P2, P3);
  and and_12 (and_12_out, P3, G2);
  and and_13 (and_13_out, P3, P2, G1);
  and and_14 (and_14_out, G0, P3, P2, P1);
  or or_1 (C1, and_1_out, G0);
  or or_2 (C2, and_2_out, and_3_out, G1);
  or or_3 (C3, and_4_out, and_5_out, G2, and_6_out);
  or or_4 (out_13, and_7_out, and_8_out, G3, and_9_out, and_10_out);
  or or_5 (Super_Generate, and_12_out, G3, and_13_out, and_14_out);

  // Notes on the sheet:
  //   C4, wordt nergens gebruikt
endmodule

module _12bit_lookahead_unit (
  input  CarryIn,
  input  P0,
  input  G0,
  input  P1,
  input  G1,
  input  P2,
  input  G2,
  output C1,
  output C2,
  output C3
);

  wire and_1_out, and_2_out, and_3_out, and_4_out, and_5_out, and_6_out;

  and and_1 (and_1_out, CarryIn, P0);
  or or_1 (C1, and_1_out, G0);
  and and_2 (and_2_out, G0, P1);
  and and_3 (and_3_out, P1, P0, CarryIn);
  and and_4 (and_4_out, P2, G1);
  and and_5 (and_5_out, P2, P1, G0);
  and and_6 (and_6_out, P2, P1, P0, CarryIn);
  or or_2 (C2, and_2_out, and_3_out, G1);
  or or_3 (C3, and_4_out, and_5_out, G2, and_6_out);
endmodule
