// Logisim project Group12.circ as structural Verilog: 3 circuits, main circuit 1bitadder
module _1bitadder (
  input  in_1,
  input  in_2,
  input  in_3,
  output out_4,
  output out_5
);

  wire and_1_out, and_2_out, and_3_out, xor_1_out;

  and and_1 (and_1_out, in_2, in_3);
  xor xor_1 (xor_1_out, in_2, in_3);
  and and_2 (and_2_out, in_1, in_2);
  and and_3 (and_3_out, in_1, in_3);
  xor xor_2 (out_4, in_1, xor_1_out);
  or or_1 (out_5, and_1_out, and_2_out, and_3_out);
endmodule

module _4_bit_adder_block (
  input  Carry_in,
  input  A0,
  input  B0,
  input  A1,
  input  B1,
  input  A2,
  input  B2,
  input  A3,
  input  B3,
  output Sum0,
  output Sum1,
  output Sum2,
  output Sum3,
  output P0,
  output G0
);

  wire and_1_out, and_2_out, and_3_out, and_4_out, and_5_out, and_6_out, and_7_out,
       modified_1bit_adder_1_generate, modified_1bit_adder_1_propagate, modified_1bit_adder_2_generate,
       modified_1bit_adder_2_propagate, modified_1bit_adder_3_generate, modified_1bit_adder_3_propagate,
       modified_1bit_adder_4_generate, modified_1bit_adder_4_propagate, or_1_out, or_2_out, or_3_out,
       p0_c0_out, p1_g0_out;

  modified_1bit_adder modified_1bit_adder_1 (
    .in_1(Carry_in), .in_2(A0), .in_3(B0), .Sum(Sum0), .Propagate(modified_1bit_adder_1_propagate),
    .Generate(modified_1bit_adder_1_generate));
  modified_1bit_adder modified_1bit_adder_2 (
    .in_1(or_1_out), .in_2(A1), .in_3(B1), .Sum(Sum1), .Propagate(modified_1bit_adder_2_propagate),
    .Generate(modified_1bit_adder_2_generate));
  modified_1bit_adder modified_1bit_adder_3 (
    .in_1(or_2_out), .in_2(A2), .in_3(B2), .Sum(Sum2), .Propagate(modified_1bit_adder_3_propagate),
    .Generate(modified_1bit_adder_3_generate));
  modified_1bit_adder modified_1bit_adder_4 (
    .in_1(or_3_out), .in_2(A3), .in_3(B3), .Sum(Sum3), .Propagate(modified_1bit_adder_4_propagate),
    .Generate(modified_1bit_adder_4_generate));
  and and_1 (and_1_out, Carry_in, modified_1bit_adder_1_propagate, modified_1bit_adder_2_propagate, modified_1bit_adder_3_propagate);
  and and_2 (and_2_out, modified_1bit_adder_1_generate, modified_1bit_adder_2_propagate, modified_1bit_adder_3_propagate);
  and and_3 (and_3_out, modified_1bit_adder_2_generate, modified_1bit_adder_3_propagate);
  and p0_c0 (p0_c0_out, Carry_in, modified_1bit_adder_1_propagate);
  and p1_g0 (p1_g0_out, modified_1bit_adder_1_generate, modified_1bit_adder_2_propagate);
  and and_4 (and_4_out, Carry_in, modified_1bit_adder_1_propagate, modified_1bit_adder_2_propagate);
  and and_5 (and_5_out, modified_1bit_adder_3_propagate, modified_1bit_adder_4_propagate, modified_1bit_adder_2_generate);
  and and_6 (and_6_out, modified_1bit_adder_4_propagate, modified_1bit_adder_3_generate);
  or or_1 (or_1_out, p0_c0_out, modified_1bit_adder_1_generate);
  or or_2 (or_2_out, p1_g0_out, and_4_out, modified_1bit_adder_2_generate);
  or or_3 (or_3_out, and_1_out, and_2_out, and_3_out, modified_1bit_adder_3_generate);
  and and_7 (and_7_out, modified_1bit_adder_2_propagate, modified_1bit_adder_3_propagate, modified_1bit_adder_4_propagate, modified_1bit_adder_1_generate);
  and and_8 (P0, modified_1bit_adder_1_propagate, modified_1bit_adder_2_propagate, modified_1bit_adder_3_propagate, modified_1bit_adder_4_propagate);
  or or_4 (G0, and_7_out, and_5_out, and_6_out, modified_1bit_adder_4_generate);

  // Notes on the sheet:
  //   c0
  //   g0
  //   p0
  //   g1
  //   g2
  //   g3
  //   p2*g1
  //   c1
  //   c2
  //   c3
endmodule

module modified_1bit_adder (
  input  in_1,
  input  in_2,
  input  in_3,
  output Sum,
  output Propagate,
  output Generate
);

  wire xor_1_out;

  xor xor_1 (xor_1_out, in_2, in_3);
  or or_1 (Propagate, in_2, in_3);
  and and_1 (Generate, in_2, in_3);
  xor xor_2 (Sum, in_1, xor_1_out);
endmodule
