// Logisim project Group13.circ as structural Verilog: 3 circuits, main circuit Oef 3 1bit adder
module Oef_3_1bit_adder (
  input  CarryIn,
  input  a,
  input  b,
  output sum,
  output Carry_Out
);

  wire and_1_out, and_2_out, and_3_out, and_4_out, and_5_out, and_6_out, and_7_out, not_1_out, not_2_out,
       not_3_out, not_4_out, not_5_out, not_6_out;

  not not_1 (not_1_out, b);
  and and_1 (and_1_out, a, not_1_out, not_2_out);
  not not_2 (not_2_out, CarryIn);
  not not_3 (not_3_out, a);
  not not_4 (not_4_out, CarryIn);
  and and_2 (and_2_out, not_3_out, b, not_4_out);
  or or_1 (sum, and_1_out, and_2_out, and_3_out, and_4_out);
  not not_5 (not_5_out, a);
  not not_6 (not_6_out, b);
  and and_3 (and_3_out, not_5_out, not_6_out, CarryIn);
  and and_4 (and_4_out, a, b, CarryIn);
  and and_5 (and_5_out, b, CarryIn);
  and and_6 (and_6_out, a, CarryIn);
  or or_2 (Carry_Out, and_5_out, and_6_out, and_7_out);
  and and_7 (and_7_out, a, b);
endmodule

module Oef_5 (
  input  a3,
  input  a2,
  input  a1,
  input  a0,
  input  b3,
  input  b2,
  input  b1,
  input  b0,
  input  c0,
  output [3:0] out_10,
  output P,
  output G
);

  wire and_1_out, c3_out, g0_out, g0p1_out, g1_out, g2_out, g3_out, or_2_out, or_3_out, p0_out, p0p1c0_out,
       p1_out, p2_out, p2g1_out, p2p1g0_out, p2p1p0c0_out, p3_out, p3g2_out, p3p2g1_out, p3p2p1g0_out;

  _1_bit_no_carry_out u_1_bit_no_carry_out_1 (.Carry_in(c3_out), .a(a3), .b(b3), .SUM(out_10[3]));
  _1_bit_no_carry_out u_1_bit_no_carry_out_2 (.Carry_in(or_3_out), .a(a2), .b(b2), .SUM(out_10[2]));
  _1_bit_no_carry_out u_1_bit_no_carry_out_3 (.Carry_in(or_2_out), .a(a1), .b(b1), .SUM(out_10[1]));
  _1_bit_no_carry_out u_1_bit_no_carry_out_4 (.Carry_in(c0), .a(a0), .b(b0), .SUM(out_10[0]));
  and g0 (g0_out, b0, a0);
  or p0 (p0_out, b0, a0);
  or p1 (p1_out, b1, a1);
  and g1 (g1_out, b1, a1);
  or p2 (p2_out, b2, a2);
  and g2 (g2_out, b2, a2);
  and p2g1 (p2g1_out, p2_out, g1_out);
  and and_1 (and_1_out, p0_out, c0);
  and p0p1c0 (p0p1c0_out, p0_out, c0, p1_out);
  and g0p1 (g0p1_out, g0_out, p1_out);
  and p2p1g0 (p2p1g0_out, p2_out, p1_out, g0_out);
  or p3 (p3_out, b3, a3);
  and g3 (g3_out, b3, a3);
  and p3g2 (p3g2_out, p3_out, g2_out);
  and p3p2p1g0 (p3p2p1g0_out, p3_out, p2_out, p1_out, g0_out);
  and p3p2g1 (p3p2g1_out, p3_out, p2_out, g1_out);
  and p2p1p0c0 (p2p1p0c0_out, p1_out, p0_out, p2_out, c0);
  and and_2 (P, p2_out, p3_out, p1_out, p0_out);
  or or_1 (G, g3_out, p3g2_out, p3p2g1_out, p3p2p1g0_out);
  or or_2 (or_2_out, g0_out, and_1_out);
  or or_3 (or_3_out, p0p1c0_out, g0p1_out, g1_out);
  or c3 (c3_out, p2g1_out, p2p1g0_out, p2p1p0c0_out, g2_out);

  // Notes on the sheet:
  //   c1
  //   c2
endmodule

module _1_bit_no_carry_out (
  input  Carry_in,
  input  a,
  input  b,
  output SUM
);

  wire and_1_out, and_2_out, and_3_out, and_4_out, not_1_out, not_2_out, not_3_out, not_4_out, not_5_out,
       not_6_out;

  not not_1 (not_1_out, Carry_in);
  not not_2 (not_2_out, a);
  not not_3 (not_3_out, Carry_in);
  not not_4 (not_4_out, b);
  not not_5 (not_5_out, a);
  not not_6 (not_6_out, b);
  and and_1 (and_1_out, not_1_out, not_2_out, b);
  and and_2 (and_2_out, not_3_out, a, not_4_out);
  and and_3 (and_3_out, Carry_in, not_5_out, not_6_out);
  and and_4 (and_4_out, Carry_in, a, b);
  or or_1 (SUM, and_1_out, and_2_out, and_3_out, and_4_out);
endmodule
