// Logisim project Group14.circ as structural Verilog: 4 circuits, main circuit 1-BitMultiplexer
module _1_BitMultiplexer (
  input  in_1,
  input  in_2,
  input  in_3,
  output out_4
);

  wire and_1_out, and_2_out, not_1_out;

  and and_1 (and_1_out, in_1, not_1_out);
  not not_1 (not_1_out, in_3);
  and and_2 (and_2_out, in_2, in_3);
  or or_1 (out_4, and_1_out, and_2_out);
endmodule

module _1_BitAdder (
  input  A,
  input  B,
  input  CarryIn,
  output out_4,
  output out_5
);

  wire and_1_out, and_2_out, and_3_out, and_4_out, and_5_out, and_6_out, not_1_out, not_2_out, not_3_out,
       or_1_out, xor_1_out, xor_2_out;

  not not_1 (not_1_out, A);
  not not_2 (not_2_out, B);
  not not_3 (not_3_out, CarryIn);
  xor xor_1 (xor_1_out, CarryIn, A);
  xor xor_2 (xor_2_out, B, A);
  and and_1 (and_1_out, not_2_out, not_1_out);
  and and_2 (and_2_out, B, A);
  or or_1 (or_1_out, and_1_out, and_2_out);
  and and_3 (and_3_out, B, xor_1_out);
  and and_4 (and_4_out, CarryIn, A);
  and and_5 (and_5_out, not_3_out, xor_2_out);
  and and_6 (and_6_out, CarryIn, or_1_out);
  or or_2 (out_4, and_3_out, and_4_out);
  or or_3 (out_5, and_5_out, and_6_out);

  // Notes on the sheet:
  //   CarryOut
  //   Sum
endmodule

module _4BitLookaheadAdder (
  input  [3:0] a0_3,
  input  [3:0] b0_3,
  input  c0,
  output P,
  output G,
  output [3:0] Sum
);

  wire and_1_out, and_2_out, and_3_out, and_4_out, and_5_out, and_6_out, and_7_out, and_8_out, and_9_out,
       and_10_out, and_11_out, and_12_out, c3_out, g0_out, or_1_out, or_2_out, or_3_out, or_4_out, or_5_out,
       or_6_out;

  and and_1 (and_1_out, a0_3[3], b0_3[3]);
  and and_2 (and_2_out, a0_3[2], b0_3[2]);
  and and_3 (and_3_out, a0_3[1], b0_3[1]);
  and g0 (g0_out, a0_3[0], b0_3[0]);
  or or_1 (or_1_out, a0_3[3], b0_3[3]);
  or or_2 (or_2_out, a0_3[2], b0_3[2]);
  or or_3 (or_3_out, a0_3[1], b0_3[1]);
  or or_4 (or_4_out, a0_3[0], b0_3[0]);
  and and_4 (and_4_out, c0, or_4_out);
  and and_5 (and_5_out, g0_out, or_3_out);
  and and_6 (and_6_out, or_3_out, and_4_out);
  and and_7 (and_7_out, and_3_out, or_2_out);
  and and_8 (and_8_out, or_2_out, and_6_out);
  and and_9 (and_9_out, or_2_out, or_3_out, g0_out);
  and and_10 (and_10_out, and_2_out, or_1_out);
  and and_11 (and_11_out, and_7_out, or_1_out);
  and and_12 (and_12_out, and_9_out, or_1_out);
  or c3 (c3_out, and_2_out, and_7_out, and_8_out, and_9_out);
  or or_5 (or_5_out, and_3_out, and_5_out, and_6_out);
  or or_6 (or_6_out, g0_out, and_4_out);
  _1_BitAdder u_1_bitadder_1 (.A(b0_3[0]), .B(a0_3[0]), .CarryIn(c0), .out_5(Sum[0]));  // open: out_4
  or or_7 (G, and_1_out, and_10_out, and_11_out, and_12_out);
  _1_BitAdder u_1_bitadder_2 (.A(b0_3[3]), .B(a0_3[3]), .CarryIn(c3_out), .out_5(Sum[3]));  // open: out_4
  _1_BitAdder u_1_bitadder_3 (.A(b0_3[2]), .B(a0_3[2]), .CarryIn(or_5_out), .out_5(Sum[2]));  // open: out_4
  _1_BitAdder u_1_bitadder_4 (.A(b0_3[1]), .B(a0_3[1]), .CarryIn(or_6_out), .out_5(Sum[1]));  // open: out_4
  and and_13 (P, or_1_out, or_2_out, or_3_out, or_4_out, c0);

  // Notes on the sheet:
  //   g3
  //   g2
  //   g1
  //   p3
  //   p2
  //   p1
  //   p0
  //   (p0*c0)
  //   (p1*g0)
  //   (p1*p0*c0)
  //   (p2*g1)
  //   (p2*p1*p0*c0)
  //   (p2*p1*g0)
  //   (p3*g2)
  //   (p3*p2*g1)
  //   (p3*p2*p1*g0)
  //   c2
  //   c1=g0+(p0*c0)
endmodule

module _12BitLookaheadUnit (
  input  P1,
  input  G1,
  input  P0,
  input  G0,
  output C2,
  output C1
);

  wire and_1_out, and_2_out;

  and and_1 (and_1_out, P1, G0);
  and and_2 (and_2_out, P1, P0);
  or or_1 (C1, P0, G0);
  or u_C2 (C2, and_1_out, and_2_out, G1);

  // Notes on the sheet:
  //   P1*G0
  //   P1*P0
endmodule
