// Logisim project Group15.circ as structural Verilog: 2 circuits, main circuit 4-bit CLA
module _4_bit_CLA (
  input  c0,
  input  [3:0] a,
  input  [3:0] b,
  output [3:0] SUM,
  output P,
  output G
);

  wire and_2_out, and_3_out, and_4_out, and_5_out, and_6_out, and_7_out, n1_bit_adder_1_g, n1_bit_adder_1_p,
       n1_bit_adder_2_g, n1_bit_adder_2_p, n1_bit_adder_3_g, n1_bit_adder_3_p, n1_bit_adder_4_g,
       n1_bit_adder_4_p, or_1_out, or_2_out, or_3_out;

  and and_1 (P, n1_bit_adder_1_p, n1_bit_adder_2_p, n1_bit_adder_3_p, n1_bit_adder_4_p);
  and and_2 (and_2_out, n1_bit_adder_3_p, n1_bit_adder_4_p, n1_bit_adder_2_g);
  and and_3 (and_3_out, n1_bit_adder_4_p, n1_bit_adder_3_g);
  and and_4 (and_4_out, n1_bit_adder_4_p, n1_bit_adder_3_p, n1_bit_adder_2_p, n1_bit_adder_1_g);
  and and_5 (and_5_out, c0, n1_bit_adder_1_p);
  or or_1 (or_1_out, and_5_out, n1_bit_adder_1_g);
  and and_6 (and_6_out, or_1_out, n1_bit_adder_2_p);
  or or_2 (or_2_out, and_6_out, n1_bit_adder_2_g);
  and and_7 (and_7_out, or_2_out, n1_bit_adder_3_p);
  or or_3 (or_3_out, and_7_out, n1_bit_adder_3_g);
  or or_4 (G, and_3_out, and_2_out, and_4_out, n1_bit_adder_4_g);
  _1_bit_adder u_1_bit_adder_1 (
    .A(a[0]), .B(b[0]), .Carry_In(c0), .p(n1_bit_adder_1_p), .g(n1_bit_adder_1_g), .SUM(SUM[0]));
  _1_bit_adder u_1_bit_adder_2 (
    .A(a[1]), .B(b[1]), .Carry_In(or_1_out), .p(n1_bit_adder_2_p), .g(n1_bit_adder_2_g), .SUM(SUM[1]));
  _1_bit_adder u_1_bit_adder_3 (
    .A(a[2]), .B(b[2]), .Carry_In(or_2_out), .p(n1_bit_adder_3_p), .g(n1_bit_adder_3_g), .SUM(SUM[2]));
  _1_bit_adder u_1_bit_adder_4 (
    .A(a[3]), .B(b[3]), .Carry_In(or_3_out), .p(n1_bit_adder_4_p), .g(n1_bit_adder_4_g), .SUM(SUM[3]));
endmodule

module _1_bit_adder (
  input  Carry_In,
  input  A,
  input  B,
  output SUM,
  output p,
  output g
);

  wire xor_2_out;

  and and_1 (g, B, A);
  or or_1 (p, B, A);
  xor xor_1 (SUM, Carry_In, xor_2_out);
  xor xor_2 (xor_2_out, A, B);
endmodule
