// Logisim project Group16.circ as structural Verilog: 4 circuits, main circuit Oef 3 - 1 bit full adder
module Oef_3___1_bit_full_adder (
  input  A,
  input  B,
  input  Cin,
  output S,
  output Cout
);

  wire and_1_out, and_2_out, xor_1_out;

  xor xor_1 (xor_1_out, A, B);
  and and_1 (and_1_out, A, B);
  xor xor_2 (S, xor_1_out, Cin);
  and and_2 (and_2_out, xor_1_out, Cin);
  or or_1 (Cout, and_2_out, and_1_out);
endmodule

// Propagate and generate
module Oef_5___Propagate_and_generate (
  input  c0,
  input  a0,
  input  b0,
  input  a1,
  input  b1,
  input  a2,
  input  b2,
  input  a3,
  input  b3,
  output c1,
  output c2,
  output P0,
  output c3,
  output G0
);

  wire and_2_out, g0_out, g1_out, g2_out, g3_out, p0_c0_out, p0_out, p1_c1_out, p1_out, p2_c2_out, p2_out,
       p3_g2_out, p3_out, p3_p2_g1_out;

  and u_g0 (g0_out, b0, a0);
  or u_p0 (p0_out, b0, a0);
  and g1 (g1_out, b1, a1);
  or p1 (p1_out, b1, a1);
  and g2 (g2_out, b2, a2);
  or p2 (p2_out, b2, a2);
  and g3 (g3_out, b3, a3);
  or p3 (p3_out, b3, a3);
  and p0_c0 (p0_c0_out, c0, p0_out);
  and p1_c1 (p1_c1_out, c1, p1_out);
  and p2_c2 (p2_c2_out, c2, p2_out);
  or u_c1 (c1, g0_out, p0_c0_out);
  or u_c2 (c2, g1_out, p1_c1_out);
  or u_c3 (c3, g2_out, p2_c2_out);
  and and_1 (P0, p3_out, p0_out, p1_out, p2_out);
  and and_2 (and_2_out, g0_out, p3_out, p2_out, p1_out);
  and p3_g2 (p3_g2_out, p3_out, g2_out);
  and p3_p2_g1 (p3_p2_g1_out, g1_out, p3_out, p2_out);
  or or_1 (G0, and_2_out, p3_g2_out, g3_out, p3_p2_g1_out);

  // Notes on the sheet:
  //   p3.p2.p1.p0
endmodule

module Oef_5___Full_adder_zonder_carryout (
  input  A,
  input  B,
  input  Cin,
  output S
);

  wire xor_1_out;

  xor xor_1 (xor_1_out, A, B);
  xor xor_2 (S, xor_1_out, Cin);
endmodule

module Oef_5___Carry_Lookahead_unit (
  input  c0,
  input  P0,
  input  G0,
  input  P1,
  input  G1,
  output C1,
  output C2
);

  wire and_1_out, and_2_out, and_3_out;

  and and_1 (and_1_out, P1, P0, c0);
  and and_2 (and_2_out, P1, G0);
  and and_3 (and_3_out, P0, c0);
  or or_1 (C1, G0, and_3_out);
  or or_2 (C2, G1, and_2_out, and_1_out);
endmodule
