// Logisim project Group17.circ as structural Verilog: 3 circuits, main circuit 1bit adder
module _1bit_adder (
  input  input_a,
  input  input_b,
  input  carryIn,
  output carryOut,
  output sum
);

  wire a_b_cI_out, a_b_out, a_cI_out, a_Nb_NcI_out, b_cI_out, Na_b_NcI_out, Na_Nb_cI_out, not_1_out,
       not_2_out, not_3_out, not_4_out, not_5_out, not_6_out;

  not not_1 (not_1_out, input_b);
  not not_2 (not_2_out, carryIn);
  not not_3 (not_3_out, input_a);
  not not_4 (not_4_out, carryIn);
  not not_5 (not_5_out, input_a);
  not not_6 (not_6_out, input_b);
  and a_b (a_b_out, input_a, input_b);
  and b_cI (b_cI_out, input_b, carryIn);
  and a_cI (a_cI_out, input_a, carryIn);
  and a_Nb_NcI (a_Nb_NcI_out, input_a, not_1_out, not_2_out);
  and Na_b_NcI (Na_b_NcI_out, not_3_out, input_b, not_4_out);
  and Na_Nb_cI (Na_Nb_cI_out, not_5_out, not_6_out, carryIn);
  and a_b_cI (a_b_cI_out, input_b, input_a, carryIn);
  or or_1 (carryOut, a_b_out, b_cI_out, a_cI_out);
  or or_2 (sum, a_Nb_NcI_out, Na_b_NcI_out, Na_Nb_cI_out, a_b_cI_out);

  // Notes on the sheet:
  //   1bit adder
endmodule

module multiplexor (
  input  input_a,
  input  selector,
  input  input_b,
  output \output 
);

  wire and_1_out, and_2_out, not_1_out;

  and and_1 (and_1_out, input_a, not_1_out);
  not not_1 (not_1_out, selector);
  and and_2 (and_2_out, selector, input_b);
  or or_1 (\output , and_1_out, and_2_out);

  // Notes on the sheet:
  //   Multiplexor (2x1bit)
endmodule

module _4bit_adder_block (
  input  CarryIn,
  input  input_a0,
  input  input_b0,
  input  input_a1,
  input  input_b1,
  input  input_a2,
  input  input_b2,
  input  input_a3,
  input  input_b3,
  output output_s0,
  output output_s1,
  output output_s2,
  output G0,
  output output_s3,
  output P0,
  output out_16
);

  wire and_1_out, and_2_out, and_3_out, and_4_out, and_5_out, and_6_out, and_7_out, and_8_out, and_9_out,
       and_10_out, and_11_out, and_12_out, and_13_out, and_14_out, and_16_out, and_17_out, and_18_out,
       n1bit_adder_3_carryout, not_1_out, not_2_out, not_3_out, or_1_out, or_2_out, or_3_out, or_4_out,
       or_5_out, or_6_out, or_7_out;

  or or_1 (or_1_out, input_a0, input_b0);
  and and_1 (and_1_out, input_a0, input_b0);
  or or_2 (or_2_out, input_a1, input_b1);
  and and_2 (and_2_out, input_a1, input_b1);
  or or_3 (or_3_out, input_a2, input_b2);
  and and_3 (and_3_out, input_a2, input_b2);
  or or_4 (or_4_out, input_a3, input_b3);
  and and_4 (and_4_out, input_a3, input_b3);
  _1bit_adder u_1bit_adder_1 (
    .input_a(input_a0), .input_b(input_b0), .carryIn(CarryIn), .sum(output_s0));  // open: carryOut
  and and_5 (and_5_out, or_1_out, CarryIn);
  or or_5 (or_5_out, and_1_out, and_5_out);
  _1bit_adder u_1bit_adder_2 (
    .input_a(input_a1), .input_b(input_b1), .carryIn(or_5_out), .sum(output_s1));  // open: carryOut
  and and_6 (and_6_out, or_2_out, or_1_out, CarryIn);
  and and_7 (and_7_out, or_2_out, and_1_out);
  or or_6 (or_6_out, and_2_out, and_7_out, and_6_out);
  _1bit_adder u_1bit_adder_3 (
    .input_a(input_a2), .input_b(input_b2), .carryIn(or_6_out), .carryOut(n1bit_adder_3_carryout),
    .sum(output_s2));
  and and_8 (and_8_out, or_3_out, or_2_out, and_1_out);
  and and_9 (and_9_out, or_3_out, and_2_out);
  or or_7 (or_7_out, and_3_out, and_9_out, and_8_out, and_12_out);
  _1bit_adder u_1bit_adder_4 (
    .input_a(input_a3), .input_b(input_b3), .carryIn(or_7_out), .sum(output_s3));  // open: carryOut
  not not_1 (not_1_out, input_b3);
  and and_10 (and_10_out, not_1_out, not_2_out);
  not not_2 (not_2_out, input_a3);
  and and_11 (and_11_out, input_a3, input_b3);
  and and_12 (and_12_out, or_3_out, or_1_out, or_2_out, CarryIn);
  and and_13 (and_13_out, n1bit_adder_3_carryout, and_10_out);
  not not_3 (not_3_out, n1bit_adder_3_carryout);
  and and_14 (and_14_out, not_3_out, and_11_out);
  or or_8 (out_16, and_13_out, and_14_out);
  and and_15 (P0, or_1_out, or_2_out, or_3_out, or_4_out);
  and and_16 (and_16_out, and_1_out, or_2_out, or_4_out, or_3_out);
  and and_17 (and_17_out, and_2_out, or_3_out, or_4_out);
  and and_18 (and_18_out, and_3_out, or_4_out);
  or or_9 (G0, and_16_out, and_17_out, and_18_out, and_4_out);

  // Notes on the sheet:
  //   g0 + (p0.c0)
  //   g1 + (p1.g0) + (p1.p0.c0)
  //   g2 + (p2.g1) + (p2.p1.g0) + (p2.p1.p0.c0)
  //   p3.p2.p1.p0
  //   g3 + (p3.g2) + (p3.p2.g1) + (p3.p2.p1.g0)
endmodule
