// Logisim project Group18.circ as structural Verilog: 3 circuits, main circuit 1bit-adder
module _1bit_adder (
  input  A,
  input  B,
  input  CarryIn,
  output Sum,
  output CarryOut
);

  wire and_1_out, and_2_out, and_3_out, and_4_out, and_5_out, and_6_out, and_7_out, not_1_out, not_2_out,
       not_3_out, not_4_out, not_5_out, not_6_out;

  and and_1 (and_1_out, B, CarryIn);
  and and_2 (and_2_out, A, CarryIn);
  and and_3 (and_3_out, A, B);
  not not_1 (not_1_out, B);
  not not_2 (not_2_out, CarryIn);
  not not_3 (not_3_out, A);
  and and_4 (and_4_out, A, not_1_out, not_2_out);
  and and_5 (and_5_out, not_3_out, B, not_4_out);
  not not_4 (not_4_out, CarryIn);
  not not_5 (not_5_out, A);
  not not_6 (not_6_out, B);
  and and_6 (and_6_out, not_5_out, not_6_out, CarryIn);
  and and_7 (and_7_out, A, B, CarryIn);
  or or_1 (Sum, and_4_out, and_5_out, and_6_out, and_7_out);
  or or_2 (CarryOut, and_1_out, and_2_out, and_3_out);
endmodule

module _4_bit_adder (
  input  C0,
  input  A0,
  input  A1,
  input  A2,
  input  A3,
  input  B0,
  input  B1,
  input  B2,
  input  B3,
  output S0,
  output S1,
  output S2,
  output S3,
  output G0,
  output P0
);

  wire and_1_out, and_2_out, and_3_out, and_4_out, and_5_out, and_6_out, and_7_out, and_8_out, and_9_out,
       and_10_out, and_11_out, and_12_out, and_13_out, or_1_out, or_2_out, or_3_out, or_4_out, or_5_out,
       or_6_out, or_7_out;

  and and_1 (and_1_out, B2, A2);
  or or_1 (or_1_out, A2, B2);
  and and_2 (and_2_out, B3, A3);
  or or_2 (or_2_out, A3, B3);
  and and_3 (and_3_out, B0, A0);
  or or_3 (or_3_out, A0, B0);
  and and_4 (and_4_out, B1, A1);
  or or_4 (or_4_out, A1, B1);
  and and_5 (and_5_out, and_3_out, or_4_out);
  and and_6 (and_6_out, and_4_out, or_1_out);
  and and_7 (and_7_out, and_1_out, or_2_out);
  and and_8 (and_8_out, and_5_out, or_1_out);
  and and_9 (and_9_out, and_6_out, or_2_out);
  and and_10 (and_10_out, C0, or_3_out);
  and and_11 (and_11_out, and_10_out, or_4_out);
  and and_12 (and_12_out, and_3_out, or_4_out, or_1_out, or_2_out);
  and and_13 (and_13_out, and_11_out, or_1_out);
  or or_5 (or_5_out, and_3_out, and_10_out);
  or or_6 (or_6_out, and_4_out, and_5_out, and_11_out);
  or or_7 (or_7_out, and_1_out, and_8_out, and_6_out, and_13_out);
  or or_8 (G0, and_2_out, and_7_out, and_9_out, and_12_out);
  and and_14 (P0, or_3_out, or_4_out, or_1_out, or_2_out);
  _1bit_adder u_1bit_adder_1 (.A(A0), .B(B0), .CarryIn(C0), .Sum(S0));  // open: CarryOut
  _1bit_adder u_1bit_adder_2 (.A(A1), .B(B1), .CarryIn(or_5_out), .Sum(S1));  // open: CarryOut
  _1bit_adder u_1bit_adder_3 (.A(A2), .B(B2), .CarryIn(or_6_out), .Sum(S2));  // open: CarryOut
  _1bit_adder u_1bit_adder_4 (.A(A3), .B(B3), .CarryIn(or_7_out), .Sum(S3));  // open: CarryOut

  // Notes on the sheet:
  //   C1
  //   C2
  //   C3
endmodule

module carry_lookahead_unit (
  input  C,
  input  G,
  input  P,
  input  in_4,
  input  in_5,
  input  in_6,
  input  in_7,
  output out_8,
  output out_9,
  output out_10
);

  wire and_1_out, and_2_out, and_3_out, and_4_out, and_5_out, and_6_out;

  and and_1 (and_1_out, P, C);
  and and_2 (and_2_out, G, in_5);
  and and_3 (and_3_out, in_7, in_4);
  and and_4 (and_4_out, and_1_out, in_5);
  and and_5 (and_5_out, and_2_out, in_7);
  and and_6 (and_6_out, and_4_out, in_7);
  or or_1 (out_8, G, and_1_out);
  or or_2 (out_9, in_4, and_2_out, and_4_out);
  or or_3 (out_10, in_6, and_3_out, and_5_out, and_6_out);
endmodule
