// Logisim project Group02.circ as structural Verilog: 6 circuits, main circuit 1-bit Multiplexor
module _1_bit_Multiplexor (
  input  in_1,
  input  in_2,
  input  in_3,
  output out_4
);

  wire and_1_out, and_2_out;

  and and_1 (and_1_out, in_1, ~in_3);  // AND_Gate
  and and_2 (and_2_out, in_3, in_2);
  or or_1 (out_4, and_1_out, and_2_out);
endmodule

module _1_bit_Full_Adder (
  input  in_1,
  input  B,
  input  in_3,
  output out_4,
  output CarryOut
);

  wire and_1_out, and_2_out, and_3_out, and_4_out, and_5_out, and_6_out, and_7_out;

  and and_1 (and_1_out, in_1, ~B, ~in_3);  // AND_Gate
  and and_2 (and_2_out, ~in_1, B, ~in_3);  // AND_Gate
  and and_3 (and_3_out, ~in_1, ~B, in_3);  // AND_Gate
  and and_4 (and_4_out, in_1, B, in_3);
  and and_5 (and_5_out, B, in_3);
  and and_6 (and_6_out, in_1, in_3);
  and and_7 (and_7_out, in_1, B);
  or or_1 (out_4, and_1_out, and_2_out, and_3_out, and_4_out);
  or or_2 (CarryOut, and_5_out, and_6_out, and_7_out);

  // Notes on the sheet:
  //   A
  //   CarryIn
  //   Output
endmodule

module _4_bit_Ripple_Carry_Adder (
  input  CarryIn,
  input  A,
  input  in_3,
  input  in_4,
  input  in_5,
  input  B,
  input  in_7,
  input  in_8,
  input  in_9,
  output out_10,
  output out_11,
  output out_12,
  output out_13,
  output out_14
);

  wire n1_bit_full_adder_1_carryout, n1_bit_full_adder_2_carryout, n1_bit_full_adder_3_carryout;

  _1_bit_Full_Adder u_1_bit_full_adder_1 (
    .in_1(A), .B(B), .in_3(CarryIn), .out_4(out_10), .CarryOut(n1_bit_full_adder_1_carryout));
  _1_bit_Full_Adder u_1_bit_full_adder_2 (
    .in_1(in_3), .B(in_7), .in_3(n1_bit_full_adder_1_carryout), .out_4(out_11),
    .CarryOut(n1_bit_full_adder_2_carryout));
  _1_bit_Full_Adder u_1_bit_full_adder_3 (
    .in_1(in_4), .B(in_8), .in_3(n1_bit_full_adder_2_carryout), .out_4(out_12),
    .CarryOut(n1_bit_full_adder_3_carryout));
  _1_bit_Full_Adder u_1_bit_full_adder_4 (
    .in_1(in_5), .B(in_9), .in_3(n1_bit_full_adder_3_carryout), .out_4(out_13), .CarryOut(out_14));
endmodule

module _4_bit_Lookahead_Adder_Block (
  input  CarryIn,
  input  [3:0] in_2,
  input  [3:0] in_3,
  output [3:0] out_4,
  output P0,
  output G0
);

  wire and_1_out, and_2_out, and_3_out, and_4_out, and_5_out, and_6_out, and_8_out, and_9_out, and_10_out,
       c1_out, c2_out, c3_out, g0_out, g1_out, g2_out, g3_out, or_1_out, or_2_out, or_3_out, or_4_out;

  or or_1 (or_1_out, in_2[3], in_3[3]);
  or or_2 (or_2_out, in_2[2], in_3[2]);
  or or_3 (or_3_out, in_2[1], in_3[1]);
  or or_4 (or_4_out, in_2[0], in_3[0]);
  and g3 (g3_out, in_2[3], in_3[3]);
  and g2 (g2_out, in_2[2], in_3[2]);
  and and_1 (and_1_out, or_2_out, g1_out);
  and and_2 (and_2_out, or_2_out, or_3_out, g0_out);
  and and_3 (and_3_out, or_2_out, or_3_out, or_4_out, CarryIn);
  and g1 (g1_out, in_2[1], in_3[1]);
  and and_4 (and_4_out, or_3_out, g0_out);
  and and_5 (and_5_out, or_3_out, or_4_out, CarryIn);
  and u_g0 (g0_out, in_2[0], in_3[0]);
  and and_6 (and_6_out, or_4_out, CarryIn);
  or c3 (c3_out, g2_out, and_1_out, and_2_out, and_3_out);
  or c2 (c2_out, g1_out, and_4_out, and_5_out);
  or c1 (c1_out, g0_out, and_6_out);
  and and_7 (P0, or_4_out, or_3_out, or_2_out, or_1_out);
  and and_8 (and_8_out, or_1_out, g2_out);
  and and_9 (and_9_out, or_1_out, or_2_out, g1_out);
  and and_10 (and_10_out, or_1_out, or_2_out, or_3_out, g0_out);
  _1_bit_Full_Adder u_1_bit_full_adder_1 (
    .in_1(in_2[3]), .B(in_3[3]), .in_3(c3_out), .out_4(out_4[3]));  // open: CarryOut
  _1_bit_Full_Adder u_1_bit_full_adder_2 (
    .in_1(in_2[2]), .B(in_3[2]), .in_3(c2_out), .out_4(out_4[2]));  // open: CarryOut
  _1_bit_Full_Adder u_1_bit_full_adder_3 (
    .in_1(in_2[1]), .B(in_3[1]), .in_3(c1_out), .out_4(out_4[1]));  // open: CarryOut
  _1_bit_Full_Adder u_1_bit_full_adder_4 (
    .in_1(in_2[0]), .B(in_3[0]), .in_3(CarryIn), .out_4(out_4[0]));  // open: CarryOut
  or or_5 (G0, g3_out, and_8_out, and_9_out, and_10_out);

  // Notes on the sheet:
  //   p3
  //   p2
  //   p1
  //   p0
endmodule

module _4_bit_Ripple_Carry_Adder__Overflow_fix (
  input  CarryIn,
  input  A,
  input  in_3,
  input  in_4,
  input  in_5,
  input  B,
  input  in_7,
  input  in_8,
  input  in_9,
  output out_10,
  output out_11,
  output out_12,
  output out_13,
  output out_14
);

  wire n1_bit_full_adder_1_carryout, n1_bit_full_adder_2_carryout;

  _1_bit_Full_Adder u_1_bit_full_adder_1 (
    .in_1(A), .B(B), .in_3(CarryIn), .out_4(out_10), .CarryOut(n1_bit_full_adder_1_carryout));
  _1_bit_Full_Adder u_1_bit_full_adder_2 (
    .in_1(in_3), .B(in_7), .in_3(n1_bit_full_adder_1_carryout), .out_4(out_11),
    .CarryOut(n1_bit_full_adder_2_carryout));
  _1_bit_Full_Adder u_1_bit_full_adder_3 (
    .in_1(in_4), .B(in_8), .in_3(n1_bit_full_adder_2_carryout), .out_4(out_12), .CarryOut(out_14));
  _1_bit_Full_Adder u_1_bit_full_adder_4 (.in_1(in_5), .B(in_9), .in_3(out_14), .out_4(out_13));  // open: CarryOut
endmodule

module Carry_Lookahead_Unit__12_bit (
  input  in_1,
  input  in_2,
  input  in_3,
  input  in_4,
  input  in_5,
  output out_6,
  output out_7
);

  wire and_1_out, and_2_out, and_3_out;

  and and_1 (and_1_out, in_1, in_2);
  or or_1 (out_6, and_1_out, in_3);
  and and_2 (and_2_out, in_4, in_3);
  and and_3 (and_3_out, in_4, in_2, in_1);
  or or_2 (out_7, and_2_out, and_3_out, in_5);

  // Notes on the sheet:
  //   C0
  //   P0
  //   G0
  //   C1
  //   P1
  //   G1
  //   C2
endmodule
