// Logisim project test2.circ as structural Verilog: 1 circuit, main circuit 1-bit adder for 4-bit
module _1_bit_adder_for_4_bit (
  input  Carry_in,
  input  A,
  input  B,
  output Sum,
  output Generate,
  output Propagate
);

  wire xor_1_out;

  xor xor_1 (xor_1_out, A, B);
  and and_1 (Generate, A, B);
  or or_1 (Propagate, A, B);
  xor xor_2 (Sum, Carry_in, xor_1_out);
endmodule
