// Logisim project test.circ as structural Verilog: 1 circuit, main circuit main
module main (
);

  wire and_1_out, and_2_out, and_3_out, or_1_out, or_2_out, or_3_out;

  buf or_1 (or_1_out, and_1_out);  // OR_Gate
  // AND_Gate and_1 has open pins: out=and_1_out
  buf or_2 (or_2_out, and_2_out);  // OR_Gate
  // AND_Gate and_2 has open pins: out=and_2_out
  buf or_3 (or_3_out, and_3_out);  // OR_Gate
  // AND_Gate and_3 has open pins: out=and_3_out
  // AND_Gate and_4 has open pins: in0=and_1_out, in1=or_1_out, out=open
  // AND_Gate and_5 has open pins: in0=and_2_out, in1=or_2_out, out=open
  // AND_Gate and_6 has open pins: in0=and_3_out, in1=or_3_out, out=open
endmodule
