// Logisim project test.circ as structural Verilog: 1 circuit, main circuit main
module main (
  input  in_1,
  input  in_2
);

  // AND_Gate and_1 has open pins: in0=in_1, in1=in_1, out=open
  // AND_Gate and_2 has open pins: in0=in_2, in1=in_2, out=open
endmodule
