// Logisim project test.circ as structural Verilog: 1 circuit, main circuit main
module main (
  input  A,
  input  B,
  input  Carry,
  input  A_2,
  input  B_2,
  input  Carry_2,
  output S,
  output S_2
);

  wire and_1_out, and_2_out, and_3_out, and_4_out, and_5_out, and_6_out, and_7_out, and_8_out;

  and and_1 (and_1_out, A, ~B, ~Carry);  // AND_Gate
  and and_2 (and_2_out, ~A, B, ~Carry);  // AND_Gate
  and and_3 (and_3_out, ~A, ~B, Carry);  // AND_Gate
  and and_4 (and_4_out, A, B, Carry);
  and and_5 (and_5_out, A_2, ~B_2, ~Carry_2);  // AND_Gate
  and and_6 (and_6_out, ~A_2, B_2, ~Carry_2);  // AND_Gate
  and and_7 (and_7_out, ~A_2, ~B_2, Carry_2);  // AND_Gate
  and and_8 (and_8_out, A_2, B_2, Carry_2);
  or or_1 (S, and_1_out, and_2_out, and_3_out, and_4_out);
  or or_2 (S_2, and_5_out, and_6_out, and_7_out, and_8_out);
endmodule
