// Logisim project Group01.circ as structural Verilog: 2 circuits, main circuit 1 bit adder
module _1_bit_adder (
  input  Carry_in,
  input  A,
  input  B,
  output S,
  output Carry_out
);

  wire and_1_out, and_2_out, and_3_out, and_4_out, and_5_out, and_6_out, and_7_out;

  and and_1 (and_1_out, Carry_in, ~A, ~B);  // AND_Gate
  and and_2 (and_2_out, ~Carry_in, A, ~B);  // AND_Gate
  and and_3 (and_3_out, ~Carry_in, ~A, B);  // AND_Gate
  and and_4 (and_4_out, ~Carry_in, A, B);  // AND_Gate
  and and_5 (and_5_out, Carry_in, A, B);
  and and_6 (and_6_out, Carry_in, A, ~B);  // AND_Gate
  and and_7 (and_7_out, Carry_in, ~A, B);  // AND_Gate
  or or_1 (S, and_1_out, and_2_out, and_3_out, and_5_out);
  or or_2 (Carry_out, and_4_out, and_5_out, and_6_out, and_7_out);
endmodule

module carry_calculation (
  input  Carry_in,
  input  a,
  input  b,
  output g,
  output p,
  output Carry_next
);

  wire and_2_out;

  and and_1 (g, a, b);
  or or_1 (p, a, b);
  and and_2 (and_2_out, p, Carry_in);
  or or_2 (Carry_next, and_2_out, g);
endmodule
