// Logisim project Group02.circ as structural Verilog: 3 circuits, main circuit 1-bit Multiplexor
module _1_bit_Multiplexor (
  input  in_1,
  input  in_2,
  input  in_3,
  output out_4
);

  wire and_1_out, and_2_out;

  and and_1 (and_1_out, in_1, ~in_3);  // AND_Gate
  and and_2 (and_2_out, in_3, in_2);
  or or_1 (out_4, and_1_out, and_2_out);
endmodule

module _1_bit_Full_Adder (
  input  in_1,
  input  B,
  input  in_3,
  output out_4,
  output CarryOut
);

  wire and_1_out, and_2_out, and_3_out, and_4_out, and_5_out, and_6_out, and_7_out;

  and and_1 (and_1_out, in_1, ~B, ~in_3);  // AND_Gate
  and and_2 (and_2_out, ~in_1, B, ~in_3);  // AND_Gate
  and and_3 (and_3_out, ~in_1, ~B, in_3);  // AND_Gate
  and and_4 (and_4_out, in_1, B, in_3);
  and and_5 (and_5_out, B, in_3);
  and and_6 (and_6_out, in_1, in_3);
  and and_7 (and_7_out, in_1, B);
  or or_1 (out_4, and_1_out, and_2_out, and_3_out, and_4_out);
  or or_2 (CarryOut, and_5_out, and_6_out, and_7_out);

  // Notes on the sheet:
  //   A
  //   CarryIn
  //   Output
endmodule

module Carry_Lookahead_Unit__12_bit (
  input  in_1,
  input  in_2,
  input  in_3,
  input  in_4,
  input  in_5,
  output out_6,
  output out_7
);

  wire and_1_out, and_2_out, and_3_out;

  and and_1 (and_1_out, in_1, in_2);
  or or_1 (out_6, and_1_out, in_3);
  and and_2 (and_2_out, in_4, in_3);
  and and_3 (and_3_out, in_4, in_2, in_1);
  or or_2 (out_7, and_2_out, and_3_out, in_5);

  // Notes on the sheet:
  //   C0
  //   P0
  //   G0
  //   C1
  //   P1
  //   G1
  //   C2
endmodule
