// Logisim project test1.circ as structural Verilog: 1 circuit, main circuit adder no carryout
module adder_no_carryout (
  input  Pin_311,
  input  Pin_312,
  input  Pin_313,
  output Pin_314
);

  wire AND_Gate_276_out, AND_Gate_277_out, AND_Gate_278_out, AND_Gate_279_out, NOT_Gate_27_out,
       NOT_Gate_28_out, NOT_Gate_29_out, NOT_Gate_30_out, NOT_Gate_31_out, NOT_Gate_32_out;

  not NOT_Gate_28 (NOT_Gate_28_out, Pin_311);
  and AND_Gate_276 (AND_Gate_276_out, NOT_Gate_28_out, NOT_Gate_32_out, Pin_313);
  not NOT_Gate_32 (NOT_Gate_32_out, Pin_312);
  not NOT_Gate_31 (NOT_Gate_31_out, Pin_311);
  and AND_Gate_278 (AND_Gate_278_out, NOT_Gate_31_out, Pin_312, NOT_Gate_27_out);
  not NOT_Gate_27 (NOT_Gate_27_out, Pin_313);
  and AND_Gate_277 (AND_Gate_277_out, Pin_311, NOT_Gate_30_out, NOT_Gate_29_out);
  not NOT_Gate_30 (NOT_Gate_30_out, Pin_312);
  not NOT_Gate_29 (NOT_Gate_29_out, Pin_313);
  and AND_Gate_279 (AND_Gate_279_out, Pin_311, Pin_312, Pin_313);
  or OR_Gate_116 (Pin_314, AND_Gate_276_out, AND_Gate_278_out, AND_Gate_277_out, AND_Gate_279_out);
endmodule
