// Logisim project test2.circ as structural Verilog: 1 circuit, main circuit 1-bit no carry out
module _1_bit_no_carry_out (
  input  Pin_407,
  input  Pin_410,
  input  Pin_409,
  output Pin_408
);

  wire AND_Gate_359_out, AND_Gate_360_out, AND_Gate_361_out, AND_Gate_362_out, NOT_Gate_39_out,
       NOT_Gate_40_out, NOT_Gate_41_out, NOT_Gate_42_out, NOT_Gate_43_out, NOT_Gate_44_out;

  not NOT_Gate_44 (NOT_Gate_44_out, Pin_407);
  not NOT_Gate_40 (NOT_Gate_40_out, Pin_410);
  not NOT_Gate_39 (NOT_Gate_39_out, Pin_407);
  not NOT_Gate_41 (NOT_Gate_41_out, Pin_409);
  not NOT_Gate_43 (NOT_Gate_43_out, Pin_410);
  not NOT_Gate_42 (NOT_Gate_42_out, Pin_409);
  and AND_Gate_362 (AND_Gate_362_out, NOT_Gate_44_out, NOT_Gate_40_out, Pin_409);
  and AND_Gate_360 (AND_Gate_360_out, NOT_Gate_39_out, Pin_410, NOT_Gate_41_out);
  and AND_Gate_359 (AND_Gate_359_out, Pin_407, NOT_Gate_43_out, NOT_Gate_42_out);
  and AND_Gate_361 (AND_Gate_361_out, Pin_407, Pin_410, Pin_409);
  or OR_Gate_154 (Pin_408, AND_Gate_362_out, AND_Gate_360_out, AND_Gate_359_out, AND_Gate_361_out);
endmodule
