// Logisim project canonical.circ as structural Verilog: 1 circuit, main circuit main
module main (
  input  in_1,
  input  in_2,
  input  in_3,
  input  in_4,
  input  in_5,
  input  in_6,
  input  in_7,
  input  in_8,
  input  in_9,
  input  in_10
);

  wire and_1_out, and_2_out, or_1_out, or_2_out;

  and and_1 (and_1_out, in_8, in_9);
  or or_1 (or_1_out, in_2, and_2_out);
  and and_2 (and_2_out, in_3, in_4);
  or or_2 (or_2_out, in_7, and_1_out);
  // AND_Gate and_3 has open pins: in0=in_1, in1=or_1_out, out=open
  // OR_Gate or_3 has open pins: in0=or_1_out, in1=in_5, out=open
  // OR_Gate or_4 has open pins: in0=in_6, in1=or_2_out, out=open
  // AND_Gate and_4 has open pins: in0=or_2_out, in1=in_10, out=open
endmodule
