// Logisim project narrow_gates.circ as structural Verilog: 1 circuit, main circuit main
module main (
);

  wire undriven;

  // AND_Gate and_1 is placed but not wired
  // AND_Gate and_2 is placed but not wired
  // AND_Gate and_3 is placed but not wired
  // AND_Gate and_4 is placed but not wired
  // AND_Gate and_5 is placed but not wired
  // AND_Gate and_6 is placed but not wired
  // AND_Gate and_7 is placed but not wired
  // OR_Gate or_1 is placed but not wired
  // NAND_Gate nand_1 is placed but not wired
  // NOR_Gate nor_1 has open pins: in0=undriven, out=open
  // XOR_Gate xor_1 is placed but not wired
  // XNOR_Gate xnor_1 is placed but not wired
endmodule
