// Logisim project overlappingClones.circ as structural Verilog: 1 circuit, main circuit main
module main (
  input  in_1,
  input  in_2,
  input  in_3,
  input  in_4,
  input  in_5,
  input  in_6,
  output out_7,
  output out_8
);

  and and_1 (out_7, in_1, in_2);
  and and_2 (out_8, in_3, in_4);
  // AND_Gate and_3 has open pins: in0=in_5, in1=in_6, out=open
endmodule
